// Logisim project cpu.circ as structural Verilog: 24 circuits, main circuit main
module \reg  (
  input  [15:0] Din,
  input  EN_X_low,
  input  EN_Y_low,
  input  RST,
  input  EN_Z_low,
  input  LOAD_low,
  input  CLK_low,
  output [15:0] Xout,
  output [15:0] Yout,
  output [15:0] Zout,
  output [15:0] out_11
);

  wire nor_1_out, not_1_out, not_2_out, not_3_out;

  nor nor_1 (nor_1_out, EN_X_low, LOAD_low, CLK_low);
  Register #(.width(16)) register_1 (.D(Din), .clk(nor_1_out), .Q(out_11), .clr(RST));  // open: en
  not not_1 (not_1_out, EN_X_low);
  not not_2 (not_2_out, EN_Y_low);
  not not_3 (not_3_out, EN_Z_low);
  assign Xout = not_1_out ? out_11 : 16'bz;  // Controlled_Buffer controlled_buffer_1
  assign Yout = not_2_out ? out_11 : 16'bz;  // Controlled_Buffer controlled_buffer_2
  assign Zout = not_3_out ? out_11 : 16'bz;  // Controlled_Buffer controlled_buffer_3

  // Notes on the sheet:
  //   Single User Register
endmodule

module main (
  input  IRQ0,
  input  IRQ1,
  input  IRQ2,
  input  IRQ3
);

  wire ALU_EN_D, ALU_SEL_SRC, Cin, CLK, CLK_low, EN_CAUSE, EN_CONTEXT, EN_ERET, EN_EXC_ADDR, EN_ISR,
       EN_STATUS, EN_X, ILL_INST, INC_PC, IO_BYTE, IO_DATA, IO_LOAD, IO_STORE, IO_USER, LD_CAUSE, LD_CONTEXT,
       LD_ERET, LD_EXC_ADDR, LD_IMM, LD_INST, LD_PTB, LD_STATUS, LD_TIMER, MMU_DATA, MMU_EN, MMU_SRC, MMU_ST,
       MODE, PG_FLT, REG_LOAD, REG_X_SRC, RESET, RO_FLT, STATUS_SRC;
  wire [2:0] ALU_SEL, SEL_X;
  wire [3:0] ALU_STATUS, multiplexer_4_out, reg_tristate_4bit_1_out_7, STATUS;
  wire [7:0] CAUSE_out_6, CAUSE_out_7;
  wire [7:4] CAUSE;
  wire [8:0] MICROCODE_ADDR;
  wire [15:0] A_BUS, CONTEXT_out_7, D_BUS, ERET_REG_out_7, EXC_ADDR_out_7, IMM, INST, INST_out_7,
       multiplexer_3_out, PC, registers_1_yout, registers_1_zout, TIMER_data, V_ADDR;
  wire [15:4] undriven;
  wire [22:0] mmu_1_a_phys;

  Multiplexer #(.width(3), .enable("false")) multiplexer_1 (
    .in0(INST[2:0]), .in1(3'b110), .out(SEL_X), .sel(REG_X_SRC));
  Multiplexer #(.width(3), .enable("false")) multiplexer_2 (
    .in0(INST[11:9]), .in1(3'b110), .out(ALU_SEL), .sel(ALU_SEL_SRC));
  Priority_Encoder priority_encoder_1 (
    .in0(1'b1), .in1(CAUSE[4]), .in2(RO_FLT), .in3(PG_FLT), .in4(ILL_INST), .out(CAUSE[7:5]));  // open: in5, in6, in7, en_in, gs, en_out
  Multiplexer #(.width(16), .enable("false")) multiplexer_3 (
    .in0(PC), .in1(A_BUS), .out(multiplexer_3_out), .sel(MMU_SRC));
  // Probe on {CAUSE, IRQ3, IRQ2, IRQ1, IRQ0}
  // Probe on CAUSE[7:5]
  mmu mmu_1 (
    .D_IN(D_BUS), .A_IN(multiplexer_3_out), .IO_LOAD(IO_LOAD), .IO_STORE(IO_STORE), .IO_USER(IO_USER),
    .IO_DATA(IO_DATA), .LD_PTB(LD_PTB), .MMU_DATA(MMU_DATA), .MMU_ST(MMU_ST), .MMU_EN(MMU_EN), .RESET(RESET),
    .CLK(CLK), .D_OUT(D_BUS), .A_PHYS(mmu_1_a_phys), .PAGE_FAULT(PG_FLT), .RO_FAULT(RO_FLT));
  // Probe on mmu_1_a_phys
  // Probe on D_BUS
  Button button_1 (.out(RESET));
  // Probe on A_BUS
  // Probe on PC
  mmio mmio_1 (
    .D_IN(D_BUS), .Dout(D_BUS), .PHYS_ADDR(mmu_1_a_phys), .IO_LOAD(IO_LOAD), .IO_STORE(IO_STORE),
    .IO_BYTE(IO_BYTE), .IO_USER(IO_DATA), .IO_DATA(IO_USER), .Clk(CLK));
  // Probe on MICROCODE_ADDR
  LED led_1 (.in(MODE));
  LED led_2 (.in(CLK));
  control control_1 (
    .INST(INST), .STATUS(STATUS), .CAUSE({CAUSE, IRQ3, IRQ2, IRQ1, IRQ0}), .ALU_Cin(Cin),
    .EN_ALU_D(ALU_EN_D), .ALU_SEL_SRC(ALU_SEL_SRC), .REG_LOAD(REG_LOAD), .EN_REG_X(EN_X),
    .REG_X_SRC(REG_X_SRC), .INC_PC(INC_PC), .LD_IMM(IO_DATA), .IO_STORE(IO_USER), .IO_LOAD(IO_STORE),
    .IO_DATA(IO_LOAD), .IO_USER(IO_BYTE), .IO_BYTE(MMU_DATA), .MMU_DATA(MMU_EN), .MMU_ST(MMU_ST),
    .MMU_EN(MMU_SRC), .MMU_SRC(LD_PTB), .LD_PTB(LD_IMM), .STATUS_SRC(LD_INST), .EN_STATUS(LD_CAUSE),
    .LD_STATUS(EN_CAUSE), .LD_INST(STATUS_SRC), .LD_TIMER(EN_STATUS), .LD_EXC_ADDR(LD_STATUS),
    .EN_EXC_ADDR(LD_EXC_ADDR), .LD_ERET(EN_EXC_ADDR), .EN_ERET(LD_ERET), .LD_CONTEXT(EN_ERET),
    .EN_CONTEXT(LD_TIMER), .EN_ISR(EN_ISR), .LD_CAUSE(LD_CONTEXT), .EN_CAUSE(EN_CONTEXT), .CLK(CLK),
    .CLK_x(CLK_low), .RESET(RESET), .ILLEGAL_INST(ILL_INST), .out_8(MICROCODE_ADDR), .MODE(MODE));
  // Probe on SEL_X
  registers registers_1 (
    .Din(D_BUS), .LOAD(REG_LOAD), .CLK_low(CLK_low), .RST(RESET), .SEL_X(SEL_X), .INC_PC(INC_PC),
    .LD_IMM16(LD_IMM), .SEL_Y(INST[5:3]), .SEL_Z(INST[8:6]), .EN_X(EN_X), .Xout(D_BUS), .PCout(PC),
    .Yout(registers_1_yout), .Zout(registers_1_zout), .IMM(IMM));
  // Probe on INST[8:6]
  // Probe on INST[5:3]
  alu_16_bit alu_16_bit_1 (
    .Y(registers_1_yout), .Z(registers_1_zout), .Cin(Cin), .ALU_SEL(ALU_SEL), .EN_D(ALU_EN_D), .d_out(D_BUS),
    .alu_status(ALU_STATUS), .a_out(A_BUS));
  // Probe on ALU_SEL
  reg_tristate u_INST (.Din(D_BUS), .LD(LD_INST), .CLK(CLK), .RST(RESET), .out_7(INST_out_7), .EN(1'b1), .Dout(INST));
  // Probe on INST_out_7
  reg_8bit_tristate u_CAUSE (
    .in_1({CAUSE, IRQ3, IRQ2, IRQ1, IRQ0}), .LD(LD_CAUSE), .CLK(CLK), .RST(RESET), .out_7(CAUSE_out_7),
    .EN(EN_CAUSE), .out_6(CAUSE_out_6));
  // Probe on CAUSE_out_7
  reg_tristate ERET_REG (
    .Din(PC), .LD(LD_ERET), .CLK(CLK), .RST(RESET), .out_7(ERET_REG_out_7), .EN(EN_ERET), .Dout(D_BUS));
  // Probe on ERET_REG_out_7
  Multiplexer #(.width(4), .enable("false")) multiplexer_4 (
    .in0(ALU_STATUS), .in1(D_BUS[3:0]), .out(multiplexer_4_out), .sel(STATUS_SRC));
  Pull_Resistor pull_resistor_1 (.node(multiplexer_4_out));
  assign D_BUS = EN_ISR ? 16'hbeef : 16'bz;  // Controlled_Buffer controlled_buffer_1
  reg_tristate_4bit reg_tristate_4bit_1 (
    .Din(multiplexer_4_out), .LD(LD_STATUS), .CLK(CLK), .RST(RESET), .out_7(reg_tristate_4bit_1_out_7),
    .EN(1'b1), .Dout(STATUS));
  // Probe on reg_tristate_4bit_1_out_7
  assign D_BUS = EN_STATUS ? {undriven, STATUS} : 16'bz;  // Controlled_Buffer controlled_buffer_2
  counter_16_bit TIMER (
    .Din(D_BUS), .LD_TIMER(LD_TIMER), .CLK(CLK), .RST(RESET), .DECR(MODE), .CARRY(CAUSE[4]), .DATA(TIMER_data));
  // Probe on TIMER_data
  reg_tristate EXC_ADDR (
    .Din(V_ADDR), .LD(LD_EXC_ADDR), .CLK(CLK), .RST(RESET), .out_7(EXC_ADDR_out_7), .EN(EN_EXC_ADDR),
    .Dout(D_BUS));
  // Probe on EXC_ADDR_out_7
  reg_tristate CONTEXT (
    .Din(IMM), .LD(LD_CONTEXT), .CLK(CLK), .RST(RESET), .out_7(CONTEXT_out_7), .EN(EN_CONTEXT), .Dout(D_BUS));
  // Probe on CONTEXT_out_7

  // Other names for the same wires on the sheet: CAUSE[3:0] = {IRQ3, IRQ2, IRQ1, IRQ0}; TIME_OUT = CAUSE[4];
  //   SEL_Y[2:0] = INST[5:3]; SEL_Z[2:0] = INST[8:6]

  // Notes on the sheet:
  //   Instruction Parameters
  //   Interrupts / Exceptions
  //   Overview
  //   Control Lines
  //   Data Path
  //   Special / Kernel Registers
endmodule

// REGISTERS
module registers (
  input  [15:0] Din,
  input  [2:0] SEL_X,
  input  EN_X,
  input  [2:0] SEL_Y,
  input  CLK_low,
  input  RST,
  input  INC_PC,
  input  LD_IMM16,
  input  LOAD,
  input  [2:0] SEL_Z,
  output [15:0] Xout,
  output [15:0] PCout,
  output [15:0] Yout,
  output [15:0] Zout,
  output [15:0] IMM
);

  wire decoder_1_out1, decoder_1_out2, decoder_1_out3, decoder_1_out4, decoder_1_out5, decoder_1_out6,
       decoder_1_out7, decoder_2_out1, decoder_2_out2, decoder_2_out3, decoder_2_out4, decoder_2_out5,
       decoder_2_out6, decoder_2_out7, decoder_3_out1, decoder_3_out2, decoder_3_out3, decoder_3_out4,
       decoder_3_out5, decoder_3_out6, decoder_3_out7, LOAD_t, not_2_out, not_3_out, not_4_out, not_5_out,
       not_6_out, not_7_out, not_8_out, not_9_out, not_10_out, not_11_out, not_12_out, not_13_out,
       not_14_out, not_15_out, not_16_out, not_17_out, not_18_out, not_19_out, or_1_out;
  wire [15:0] fp_out_11, IMM_out_7, pc_out_13, r1_out_11, r2_out_11, r3_out_11, sp_out_11, Xout_t;

  not not_1 (LOAD_t, LOAD);
  not not_2 (not_2_out, decoder_1_out1);
  not not_3 (not_3_out, decoder_1_out2);
  not not_4 (not_4_out, decoder_1_out3);
  not not_5 (not_5_out, decoder_1_out4);
  not not_6 (not_6_out, decoder_1_out5);
  not not_7 (not_7_out, decoder_1_out6);
  Decoder #(.select(3), .enable("false")) decoder_1 (
    .out1(decoder_1_out1), .out2(decoder_1_out2), .out3(decoder_1_out3), .out4(decoder_1_out4),
    .out5(decoder_1_out5), .out6(decoder_1_out6), .out7(decoder_1_out7), .sel(SEL_Y));  // open: out0
  \reg  r2 (
    .Din(Din), .EN_X_low(not_8_out), .EN_Y_low(not_3_out), .EN_Z_low(not_13_out), .LOAD_low(LOAD_t),
    .CLK_low(CLK_low), .RST(RST), .out_11(r2_out_11), .Xout(Xout_t), .Yout(Yout), .Zout(Zout));
  // Probe on r2_out_11
  \reg  fp (
    .Din(Din), .EN_X_low(not_11_out), .EN_Y_low(not_5_out), .EN_Z_low(not_14_out), .LOAD_low(LOAD_t),
    .CLK_low(CLK_low), .RST(RST), .out_11(fp_out_11), .Xout(Xout_t), .Yout(Yout), .Zout(Zout));
  // Probe on fp_out_11
  reg_pc pc (
    .RST(RST), .INC_PC(INC_PC), .CLK(CLK_low), .PCin(Din), .EN_X_low(not_18_out), .EN_Y_low(not_7_out),
    .EN_Z_low(not_19_out), .LOAD_low(LOAD_t), .out_13(pc_out_13), .Xout(Xout_t), .Yout(Yout), .Zout(Zout),
    .PCout(PCout));
  // Probe on pc_out_13
  Decoder #(.select(3)) decoder_2 (
    .out1(decoder_2_out1), .out2(decoder_2_out2), .out3(decoder_2_out3), .out4(decoder_2_out4),
    .out5(decoder_2_out5), .out6(decoder_2_out6), .out7(decoder_2_out7), .sel(SEL_X));  // open: out0, en
  not not_8 (not_8_out, decoder_2_out2);
  not not_9 (not_9_out, decoder_2_out3);
  not not_10 (not_10_out, decoder_2_out5);
  not not_11 (not_11_out, decoder_2_out4);
  not not_12 (not_12_out, decoder_2_out1);
  not not_13 (not_13_out, decoder_3_out2);
  not not_14 (not_14_out, decoder_3_out4);
  not not_15 (not_15_out, decoder_3_out5);
  not not_16 (not_16_out, decoder_3_out1);
  not not_17 (not_17_out, decoder_3_out3);
  Decoder #(.select(3), .enable("false")) decoder_3 (
    .out1(decoder_3_out1), .out2(decoder_3_out2), .out3(decoder_3_out3), .out4(decoder_3_out4),
    .out5(decoder_3_out5), .out6(decoder_3_out6), .out7(decoder_3_out7), .sel(SEL_Z));  // open: out0
  not not_18 (not_18_out, decoder_2_out6);
  not not_19 (not_19_out, decoder_3_out6);
  // Probe on r1_out_11
  // Probe on r3_out_11
  // Probe on sp_out_11
  or or_1 (or_1_out, decoder_2_out7, LD_IMM16);
  \reg  r1 (
    .Din(Din), .EN_X_low(not_12_out), .EN_Y_low(not_2_out), .EN_Z_low(not_16_out), .LOAD_low(LOAD_t),
    .CLK_low(CLK_low), .RST(RST), .out_11(r1_out_11), .Xout(Xout_t), .Yout(Yout), .Zout(Zout));
  \reg  r3 (
    .Din(Din), .EN_X_low(not_9_out), .EN_Y_low(not_4_out), .EN_Z_low(not_17_out), .LOAD_low(LOAD_t),
    .CLK_low(CLK_low), .RST(RST), .out_11(r3_out_11), .Xout(Xout_t), .Yout(Yout), .Zout(Zout));
  \reg  sp (
    .Din(Din), .EN_X_low(not_10_out), .EN_Y_low(not_6_out), .EN_Z_low(not_15_out), .LOAD_low(LOAD_t),
    .CLK_low(CLK_low), .RST(RST), .out_11(sp_out_11), .Xout(Xout_t), .Yout(Yout), .Zout(Zout));
  reg_tristate u_IMM (.Din(Din), .LD(or_1_out), .CLK(CLK_low), .RST(RST), .out_7(IMM_out_7), .EN(1'b1), .Dout(IMM));
  // Probe on IMM_out_7
  assign Xout_t = decoder_2_out7 ? IMM : 16'bz;  // Controlled_Buffer controlled_buffer_1
  assign Yout = decoder_1_out7 ? IMM : 16'bz;  // Controlled_Buffer controlled_buffer_2
  assign Zout = decoder_3_out7 ? IMM : 16'bz;  // Controlled_Buffer controlled_buffer_3
  assign Xout = EN_X ? Xout_t : 16'bz;  // Controlled_Buffer controlled_buffer_4
  Pull_Resistor pull_resistor_1 (.node(Xout_t));
  Pull_Resistor pull_resistor_2 (.node(Yout));
  Pull_Resistor pull_resistor_3 (.node(Zout));

  // Notes on the sheet:
  //   Full Register Unit
endmodule

// CONTROL
module control (
  input  RESET,
  input  [15:0] INST,
  input  [3:0] STATUS,
  input  [7:0] CAUSE,
  output CLK,
  output CLK_x,
  output ILLEGAL_INST,
  output [8:0] out_8,
  output MODE,
  output ALU_Cin,
  output IO_STORE,
  output STATUS_SRC,
  output LD_EXC_ADDR,
  output EN_ALU_D,
  output IO_LOAD,
  output EN_STATUS,
  output EN_EXC_ADDR,
  output ALU_SEL_SRC,
  output IO_DATA,
  output LD_STATUS,
  output LD_ERET,
  output IO_USER,
  output LD_INST,
  output EN_ERET,
  output IO_BYTE,
  output LD_TIMER,
  output LD_CONTEXT,
  output REG_LOAD,
  output EN_CONTEXT,
  output EN_REG_X,
  output EN_ISR,
  output MMU_DATA,
  output REG_X_SRC,
  output LD_CAUSE,
  output MMU_ST,
  output INC_PC,
  output EN_CAUSE,
  output MMU_EN,
  output LD_IMM,
  output MMU_SRC,
  output LD_PTB
);

  wire and_1_out, and_2_out, and_3_out, and_4_out, and_5_out, and_6_out, and_7_out, COND_INV, COND_TRUE,
       decoder_1_out0, decoder_1_out1, decoder_1_out2, decoder_1_out3, decoder_1_out4, decoder_1_out5,
       decoder_1_out6, decoder_1_out7, FETCH, INT_PENDING, INT_VEC, KERN_ONLY, not_1_out, NOT_INT_VEC,
       or_1_out, or_2_out, or_4_out, TOGGLE_MODE, TRAP_PENDING;
  wire [1:0] pull_resistor_1_node;
  wire [2:0] COND, rom_1_data_2;
  wire [3:0] CAUSE_HI_4;
  wire [6:5] rom_2_data;
  wire [8:0] bit_extender_1_out, multiplexer_1_out, NEXT;
  wire [27:14] rom_1_data;

  Decoder #(.select(3)) decoder_1 (
    .out0(decoder_1_out0), .out1(decoder_1_out1), .out2(decoder_1_out2), .out3(decoder_1_out3),
    .out4(decoder_1_out4), .out5(decoder_1_out5), .out6(decoder_1_out6), .out7(decoder_1_out7), .sel(COND));  // open: en
  assign bit_extender_1_out = {{5{1'b1}}, CAUSE_HI_4};  // Bit_Extender bit_extender_1
  Pull_Resistor pull_resistor_1 (.node(pull_resistor_1_node));
  and and_1 (and_1_out, decoder_1_out1, STATUS[0]);
  and and_2 (and_2_out, decoder_1_out2, STATUS[1]);
  and and_3 (and_3_out, decoder_1_out3, STATUS[2]);
  and and_4 (and_4_out, decoder_1_out4, STATUS[3]);
  and and_5 (and_5_out, decoder_1_out5, or_1_out);
  or or_1 (or_1_out, STATUS[1], STATUS[0]);
  and and_6 (and_6_out, decoder_1_out6, INT_PENDING);
  and and_7 (and_7_out, decoder_1_out7, NOT_INT_VEC);
  not not_1 (not_1_out, FETCH);
  Multiplexer #(.width(9), .disabled("Z")) multiplexer_1 (
    .in0({pull_resistor_1_node, INST[15:9]}), .in1(bit_extender_1_out), .out(multiplexer_1_out),
    .sel(COND_TRUE), .en(FETCH));
  // Probe on multiplexer_1_out
  Multiplexer #(.width(9), .disabled("Z")) multiplexer_2 (
    .in0(NEXT), .in1(bit_extender_1_out), .out(multiplexer_1_out), .sel(COND_TRUE), .en(not_1_out));
  or or_2 (or_2_out, decoder_1_out0, and_1_out, and_2_out, and_3_out, and_4_out, and_5_out, and_6_out, and_7_out);
  or or_3 (NOT_INT_VEC, ~CAUSE[5], CAUSE[6], CAUSE[7]);  // OR_Gate
  or or_4 (or_4_out, CAUSE[5], CAUSE[6], CAUSE[7]);
  and and_8 (TRAP_PENDING, or_4_out, MODE);
  Register #(.width(9)) register_1 (.D(multiplexer_1_out), .clk(CLK_x), .Q(out_8), .clr(RESET));  // open: en
  xor xor_1 (COND_TRUE, or_2_out, COND_INV);
  LED led_1 (.in(CLK));
  not not_2 (INT_VEC, NOT_INT_VEC);
  ROM #(.addrWidth(9), .dataWidth(32)) rom_1 (
    .addr(out_8),
    .data({COND_INV, FETCH, MMU_EN, IO_USER, rom_1_data[27], ALU_SEL_SRC, IO_BYTE, rom_1_data[24], rom_1_data_2, LD_STATUS, STATUS_SRC, rom_1_data[18], LD_CONTEXT, LD_TIMER, rom_1_data[15:14], LD_EXC_ADDR, LD_IMM, LD_INST, LD_PTB, MMU_SRC, MMU_ST, MMU_DATA, IO_LOAD, IO_STORE, INC_PC, IO_DATA, REG_X_SRC, REG_LOAD, ALU_Cin}));
  ROM #(.addrWidth(9), .dataWidth(16)) rom_2 (.addr(out_8), .data({NEXT, rom_2_data, KERN_ONLY, TOGGLE_MODE, COND}));
  Clock clock_1 (.out(CLK));
  not not_3 (CLK_x, CLK);
  and and_9 (LD_ERET, rom_1_data[14], MODE);
  and and_10 (LD_CAUSE, rom_1_data[18], MODE);
  Decoder #(.select(3)) decoder_2 (
    .out0(EN_CONTEXT), .out1(EN_EXC_ADDR), .out2(EN_ERET), .out3(EN_ISR), .out4(EN_STATUS), .out5(EN_CAUSE),
    .out6(EN_REG_X), .out7(EN_ALU_D), .sel(rom_1_data_2), .en(rom_1_data[24]));
  J_K_Flip_Flop j_k_ff_1 (.J(TOGGLE_MODE), .K(TOGGLE_MODE), .clk(CLK), .Q(MODE), .reset(RESET));  // open: Qn, preset
  or or_5 (INT_PENDING, CAUSE[0], CAUSE[1], CAUSE[2], CAUSE[3], CAUSE[4]);
  and and_11 (ILLEGAL_INST, KERN_ONLY, MODE);

  // Other names for the same wires on the sheet: Cin = ALU_Cin; CAUSE_LO_5[4:0] = CAUSE[4:0];
  //   CAUSE_HI_3[2:0] = CAUSE[7:5]; NEG = STATUS[0]; ZERO = STATUS[1]; CARRY = STATUS[2]; OVERF = STATUS[3]

  // Notes on the sheet:
  //   Control Unit
  //   contents of rom_1 (hex, n*v repeats v):
  //   16*0 40000000 f00002 6*0 80041050 5*0 80045050 6*0 4044260 4044240 73*0 80040000 7*0 80040000 0
  //   80041050 0 80040000 80044000 131*0 4e10000 0 4f80000 800002 4c00220 4000242 4e00002 232*0 20047850
  //   14*0 60000850
  //   contents of rom_2 (hex, n*v repeats v):
  //   16*0 8381 7*0 803 5*0 8303 6*0 8283 8303 73*0 820b 7*0 800b 0 808b 0 818b 840b 130*0 4 239*0 3
  //   Registers
  //   Internal Control Lines
  //   ALU
  //   MMU
  //   External Control Lines
  //   MMIO
  //   Special
  //   Some Exception Generators
  //   Exceptions / Interrupts
endmodule

// ALU
module alu_4_bit (
  input  [3:0] Ain,
  input  [3:0] Bin,
  input  [2:0] S,
  input  Cin,
  output [3:0] Dout,
  output Cout
);

  wire [3:0] adder_1_out, and_1_out, or_1_out, subtractor_1_out, subtractor_2_out, xor_1_out;

  assign xor_1_out = Ain ^ Bin;  // XOR_Gate xor_1, 4 bits wide
  Subtractor #(.width(4)) subtractor_1 (.a(Bin), .b(Ain), .out(subtractor_1_out), .bin(Cin));  // open: bout
  assign and_1_out = Ain & Bin;  // AND_Gate and_1, 4 bits wide
  Subtractor #(.width(4)) subtractor_2 (.a(Ain), .b(Bin), .out(subtractor_2_out), .bin(Cin));  // open: bout
  assign or_1_out = Ain | Bin;  // OR_Gate or_1, 4 bits wide
  Adder #(.width(4)) adder_1 (.a(Ain), .b(Bin), .out(adder_1_out), .cin(Cin), .cout(Cout));
  Multiplexer #(.select(3), .width(4), .enable("false")) multiplexer_1 (
    .in0(4'b0000), .in1(xor_1_out), .in2(subtractor_1_out), .in3(and_1_out), .in4(subtractor_2_out),
    .in5(or_1_out), .in6(adder_1_out), .in7(4'b1111), .out(Dout), .sel(S));

  // Notes on the sheet:
  //   ALU (4 bit segment)
endmodule

// ALU
module alu_16_bit (
  input  [15:0] Y,
  input  [15:0] Z,
  input  Cin,
  input  [2:0] ALU_SEL,
  input  EN_D,
  output [15:0] d_out,
  output [3:0] alu_status,
  output [15:0] a_out
);

  wire _4_BIT_2_cout, _4_BIT_3_cout, _4_BIT_cout, and_1_out, and_2_out, EN_A, not_2_out, not_3_out, not_4_out;
  wire [2:0] _4_BIT_4_dout;
  wire [3:0] _4_BIT_2_dout, _4_BIT_3_dout, _4_BIT_dout;

  alu_4_bit _4_BIT (.Ain(Y[3:0]), .Bin(Z[3:0]), .Cin(Cin), .S(ALU_SEL), .Dout(_4_BIT_dout), .Cout(_4_BIT_cout));
  alu_4_bit _4_BIT_2 (
    .Ain(Y[7:4]), .Bin(Z[7:4]), .Cin(_4_BIT_cout), .S(ALU_SEL), .Dout(_4_BIT_2_dout), .Cout(_4_BIT_2_cout));
  alu_4_bit _4_BIT_3 (
    .Ain(Y[11:8]), .Bin(Z[11:8]), .Cin(_4_BIT_2_cout), .S(ALU_SEL), .Dout(_4_BIT_3_dout), .Cout(_4_BIT_3_cout));
  alu_4_bit _4_BIT_4 (
    .Ain(Y[15:12]), .Bin(Z[15:12]), .Cin(_4_BIT_3_cout), .S(ALU_SEL), .Dout({alu_status[0], _4_BIT_4_dout}),
    .Cout(alu_status[2]));
  not not_1 (EN_A, EN_D);
  not not_2 (not_2_out, alu_status[0]);
  and and_1 (and_1_out, not_2_out, Y[15], Z[15]);
  not not_3 (not_3_out, Y[15]);
  and and_2 (and_2_out, alu_status[0], not_3_out, not_4_out);
  not not_4 (not_4_out, Z[15]);
  assign d_out = EN_D ? {alu_status[0], _4_BIT_4_dout, _4_BIT_3_dout, _4_BIT_2_dout, _4_BIT_dout} : 16'bz;  // Controlled_Buffer controlled_buffer_1
  assign a_out = EN_A ? {alu_status[0], _4_BIT_4_dout, _4_BIT_3_dout, _4_BIT_2_dout, _4_BIT_dout} : 16'bz;  // Controlled_Buffer controlled_buffer_2
  nor nor_1 (alu_status[1], _4_BIT_dout[0], _4_BIT_dout[1], _4_BIT_dout[2], _4_BIT_dout[3], _4_BIT_2_dout[0], _4_BIT_2_dout[1], _4_BIT_2_dout[2], _4_BIT_2_dout[3], _4_BIT_3_dout[0], _4_BIT_3_dout[1], _4_BIT_3_dout[2], _4_BIT_3_dout[3], _4_BIT_4_dout[0], _4_BIT_4_dout[1], _4_BIT_4_dout[2], alu_status[0]);
  or or_1 (alu_status[3], and_1_out, and_2_out);

  // Notes on the sheet:
  //   ALU (Full 16 bit)
  //   zero
  //   neg
  //   carry
  //   over
endmodule

// MMU
module mmu (
  input  [15:0] D_IN,
  input  [15:0] A_IN,
  input  IO_LOAD,
  input  IO_STORE,
  input  IO_USER,
  input  IO_DATA,
  input  LD_PTB,
  input  MMU_DATA,
  input  MMU_ST,
  input  MMU_EN,
  input  RESET,
  input  CLK,
  output [15:0] D_OUT,
  output [22:0] A_PHYS,
  output PAGE_FAULT,
  output RO_FAULT
);

  wire and_1_out, and_2_out, nor_1_out, nor_2_out, not_1_out, not_2_out, or_1_out;
  wire [7:0] PTB_out_6, PTB_out_7;
  wire [15:14] ram_1_data;
  wire [22:9] ram_1_data_2;

  reg_8bit_tristate PTB (
    .in_1(D_IN[7:0]), .LD(LD_PTB), .CLK(CLK), .RST(RESET), .out_7(PTB_out_7), .EN(1'b1), .out_6(PTB_out_6));
  // Probe on PTB_out_7
  not not_1 (not_1_out, CLK);
  not not_2 (not_2_out, MMU_ST);
  nor nor_1 (nor_1_out, not_1_out, MMU_DATA, not_2_out);
  nor nor_2 (nor_2_out, MMU_DATA, MMU_ST);
  and and_1 (and_1_out, CLK, MMU_DATA, MMU_ST);
  and and_2 (and_2_out, MMU_DATA, not_2_out);
  RAM #(.addrWidth(16), .dataWidth(16), .trigger("high")) ram_1 (
    .addr({IO_DATA, PTB_out_6, A_IN[15:9]}), .we(nor_1_out), .oe(nor_2_out), .data({ram_1_data, ram_1_data_2}));
  RAM #(.addrWidth(16), .dataWidth(16), .trigger("high")) ram_2 (
    .addr({IO_DATA, PTB_out_6, A_IN[15:9]}), .we(and_1_out), .oe(and_2_out), .data({ram_1_data, ram_1_data_2}));
  Pull_Resistor pull_resistor_1 (.node({ram_1_data, ram_1_data_2}));
  assign D_OUT = MMU_EN ? {ram_1_data, ram_1_data_2} : 16'bz;  // Controlled_Buffer controlled_buffer_1
  assign {ram_1_data, ram_1_data_2} = MMU_ST ? D_IN : 16'bz;  // Controlled_Buffer controlled_buffer_2
  Multiplexer #(.width(23), .enable("false")) multiplexer_1 (
    .in0({{7{1'b0}}, A_IN}), .in1({ram_1_data_2, A_IN[8:0]}), .out(A_PHYS), .sel(IO_USER));
  and and_3 (PAGE_FAULT, ram_1_data[14], or_1_out);
  or or_1 (or_1_out, IO_STORE, IO_LOAD);
  and and_4 (RO_FAULT, ram_1_data[15], IO_STORE);

  // Notes on the sheet:
  //   ~DATA & MMU_ST == ~(DATA | ~MMU_ST)
  //   ~DATA & ~MMU_ST == ~(DATA | MMU_ST)
  //   DATA & MMU_ST
  //   DATA & ~MMU_ST
  //   Memory Management Unit (MMU)
  //   flags:
  //   1. No page set
  //   2. No user writes
endmodule

module reg_pc (
  input  RST,
  input  INC_PC,
  input  CLK,
  input  [15:0] PCin,
  input  EN_X_low,
  input  EN_Y_low,
  input  EN_Z_low,
  input  LOAD_low,
  output [15:0] Xout,
  output [15:0] Yout,
  output [15:0] Zout,
  output [15:0] PCout,
  output [15:0] out_13
);

  wire counter_1_carry, nor_1_out, not_1_out, not_2_out, not_3_out;
  wire [15:15] counter_1_q, pull_resistor_1_node;

  Pull_Resistor pull_resistor_1 (.node(pull_resistor_1_node[15]));
  nor nor_1 (nor_1_out, LOAD_low, EN_X_low);
  Counter #(.width(16), .max('hffff), .trigger("falling")) counter_1 (
    .clr(RST), .load(nor_1_out), .up(INC_PC), .count(INC_PC), .clk(CLK),
    .D({pull_resistor_1_node[15], PCin[15:1]}), .carry(counter_1_carry), .Q({counter_1_q[15], out_13[15:1]}));
  Pull_Resistor pull_resistor_2 (.node(out_13[0]));
  assign Xout = not_1_out ? out_13 : 16'bz;  // Controlled_Buffer controlled_buffer_1
  not not_1 (not_1_out, EN_X_low);
  assign Yout = not_2_out ? out_13 : 16'bz;  // Controlled_Buffer controlled_buffer_2
  not not_2 (not_2_out, EN_Y_low);
  assign Zout = not_3_out ? out_13 : 16'bz;  // Controlled_Buffer controlled_buffer_3
  not not_3 (not_3_out, EN_Z_low);

  assign PCout = out_13;

  // Notes on the sheet:
  //   Program Counter (PC)
endmodule

module reg_tristate (
  input  [15:0] Din,
  input  LD,
  input  CLK,
  input  RST,
  input  EN,
  output [15:0] Dout,
  output [15:0] out_7
);

  Register #(.width(16)) register_1 (.D(Din), .en(LD), .clk(CLK), .Q(out_7), .clr(RST));
  assign Dout = EN ? out_7 : 16'bz;  // Controlled_Buffer controlled_buffer_1

  // Notes on the sheet:
  //   Tristate Register (16 bit)
endmodule

module reg_8bit_tristate (
  input  [7:0] in_1,
  input  LD,
  input  CLK,
  input  RST,
  input  EN,
  output [7:0] out_6,
  output [7:0] out_7
);

  Register register_1 (.D(in_1), .en(LD), .clk(CLK), .Q(out_7), .clr(RST));
  assign out_6 = EN ? out_7 : 8'bz;  // Controlled_Buffer controlled_buffer_1

  // Notes on the sheet:
  //   Tristate Register (8 bit)
endmodule

module counter_16_bit (
  input  [15:0] Din,
  input  LD_TIMER,
  input  CLK,
  input  RST,
  input  DECR,
  output CARRY,
  output [15:0] DATA
);

  wire and_1_out, not_1_out;

  not not_1 (not_1_out, CARRY);
  and and_1 (and_1_out, not_1_out, DECR);
  Counter #(.width(16), .max('hffff)) counter_1 (
    .clr(RST), .load(LD_TIMER), .up(1'b0), .count(and_1_out), .clk(CLK), .D(Din), .carry(CARRY), .Q(DATA));
  Pull_Resistor pull_resistor_1 (.node(CARRY));
endmodule

// RAM
module ram (
  input  [15:0] Din,
  input  [23:0] ADDR,
  input  BYPASS_RAM,
  input  CLK,
  input  STORE,
  input  LOAD,
  input  BYTE,
  output [15:0] Dout
);

  wire and_2_out, and_3_out, and_4_out, and_5_out, and_6_out, and_7_out, BYPASS_RAM_t, comparator_1_eq,
       comparator_2_eq, MAP_RAM, not_1_out, not_2_out, not_4_out, not_5_out, or_1_out;
  wire [7:0] rom_1_data, rom_2_data;
  wire [15:0] ram_1_data;

  not not_1 (not_1_out, BYPASS_RAM_t);
  not not_2 (not_2_out, LOAD);
  not not_3 (MAP_RAM, comparator_1_eq);
  Comparator #(.width(16)) comparator_1 (.a(ADDR[23:8]), .b(16'h1ff), .eq(comparator_1_eq));  // open: gt, lt
  Comparator #(.width(16)) comparator_2 (.a(ADDR[23:8]), .b({16{1'b0}}), .eq(comparator_2_eq));  // open: gt, lt
  and and_1 (BYPASS_RAM_t, comparator_2_eq, BYPASS_RAM);
  and and_2 (and_2_out, not_1_out, not_2_out, STORE, MAP_RAM);
  and and_3 (and_3_out, not_1_out, MAP_RAM, LOAD);
  and and_4 (and_4_out, and_2_out, ~CLK);  // AND_Gate
  RAM #(.addrWidth(23), .trigger("high")) ram_1 (
    .addr(ADDR[23:1]), .we(and_4_out), .oe(and_3_out), .data(ram_1_data[7:0]));
  RAM #(.addrWidth(23), .trigger("high")) ram_2 (
    .addr(ADDR[23:1]), .we(and_4_out), .oe(and_3_out), .data(ram_1_data[15:8]));
  ROM rom_1 (.addr(ADDR[8:1]), .data(rom_1_data));
  ROM rom_2 (.addr(ADDR[8:1]), .data(rom_2_data));
  not not_4 (not_4_out, ADDR[0]);
  not not_5 (not_5_out, BYTE);
  and and_5 (and_5_out, not_4_out, BYTE);
  and and_6 (and_6_out, ADDR[0], BYTE);
  Pull_Resistor pull_resistor_1 (.node(ram_1_data[7:0]));
  Pull_Resistor pull_resistor_2 (.node(ram_1_data[15:8]));
  or or_1 (or_1_out, and_5_out, not_5_out);
  Multiplexer #(.width(8), .disabled("Z"), .enable("false")) multiplexer_1 (
    .in1(rom_1_data), .out(ram_1_data[7:0]), .sel(and_7_out));  // open: in0
  Multiplexer #(.width(8), .disabled("Z"), .enable("false")) multiplexer_2 (
    .in1(rom_2_data), .out(ram_1_data[15:8]), .sel(and_7_out));  // open: in0
  assign Dout[7:0] = or_1_out ? ram_1_data[7:0] : 8'bz;  // Controlled_Buffer controlled_buffer_1
  assign Dout[7:0] = and_6_out ? ram_1_data[15:8] : 8'bz;  // Controlled_Buffer controlled_buffer_2
  assign Dout[15:8] = not_5_out ? ram_1_data[15:8] : 8'bz;  // Controlled_Buffer controlled_buffer_3
  and and_7 (and_7_out, BYPASS_RAM_t, MAP_RAM, LOAD);
  Multiplexer #(.width(16), .disabled("Z"), .enable("false")) multiplexer_3 (
    .in1(Din), .out(ram_1_data), .sel(and_4_out));  // open: in0

  // Notes on the sheet:
  //   Byte Addressable RAM
  //   This RAM circuit is no longer used
  //   contents of rom_1 (hex, n*v repeats v):
  //   f8
  //   contents of rom_2 (hex, n*v repeats v):
  //   f5 1 f0
  //   This RAM unit reads unaligned bytes and aligned 16 bit words.
  //   ~BYTE | (BYTE & ADDR_0)
  //   ~BYTE
  //   BYTE & ADDR_0
  //   these muxes are operating as tristate buffers due to a strange logisim bug
endmodule

// EXT
module sign_ext (
  input  [15:0] in_1,
  input  SIGN_EXT,
  input  EN_MMIO,
  output [15:0] out_4
);

  Multiplexer #(.width(16), .disabled("Z")) multiplexer_1 (
    .in0(in_1), .in1({{9{in_1[7]}}, in_1[6:0]}), .out(out_4), .sel(SIGN_EXT), .en(EN_MMIO));
endmodule

module test (
  input  [15:0] in_1,
  input  [15:0] in_2,
  input  in_3,
  input  in_4,
  input  in_5,
  input  in_6,
  input  in_7,
  input  in_8,
  input  in_9,
  input  in_10,
  input  in_11,
  input  [4:0] in_12
);

  wire [15:0] mmio_old_1_dout;
  wire [23:0] undriven;

  // Probe on mmio_old_1_dout
  mmio_OLD mmio_old_1 (
    .Din(mmio_old_1_dout), .PhysAddr(undriven), .Load(in_12[4]), .Byte(in_12[3]), .User(in_12[2]),
    .Data(in_12[1]), .Clk(in_12[0]), .Dout(mmio_old_1_dout));  // open: Store
  // mmu mmu_1: pin names not known; wires that end beside it: in_1, in_2, in_3, in_8, in_4, in_9, in_5, in_10, in_6, in_11, in_7
endmodule

module mmio_OLD (
  input  [15:0] Din,
  input  [23:0] PhysAddr,
  input  Store,
  input  Load,
  input  Byte,
  input  User,
  input  Data,
  input  Clk,
  output [15:0] Dout
);

  wire and_4_out, and_8_out, and_10_out, and_11_out, Even, HighByte, notClk, or_2_out, or_3_out, or_4_out,
       or_5_out, PhysRAM, PhysROM, Ram0_OutEn, Ram0_WrEn, Ram1_OutEn, Ram1_WrEn, Rom0_OutEn, Rom1_OutEn, Word;
  wire [7:0] HI_8, LO_8, rom_1_data, rom_2_data;

  not not_1 (notClk, Clk);
  not not_2 (Word, Byte);
  not not_3 (Even, PhysAddr[0]);
  or or_1 (HighByte, PhysAddr[0], Word);
  or or_2 (or_2_out, PhysAddr[9], PhysAddr[10], PhysAddr[11], PhysAddr[12]);
  or or_3 (or_3_out, PhysAddr[13], PhysAddr[14], PhysAddr[15], PhysAddr[16]);
  or or_4 (or_4_out, PhysAddr[17], PhysAddr[18], PhysAddr[19], PhysAddr[19]);
  or or_5 (or_5_out, or_2_out, or_3_out, or_4_out, or_4_out);
  and and_1 (PhysRAM, or_5_out, ~PhysAddr[20]);  // AND_Gate
  // Probe on HI_8
  nor nor_1 (PhysROM, PhysRAM, PhysAddr[20]);
  RAM #(.addrWidth(20), .trigger("high")) ram_1 (.addr(PhysAddr[20:1]), .we(Ram0_WrEn), .oe(Ram0_OutEn), .data(LO_8));
  ROM rom_1 (.addr(PhysAddr[8:1]), .data(rom_1_data));
  // Probe on LO_8
  and and_2 (Rom0_OutEn, Even, Load, PhysROM);
  and and_3 (Ram0_OutEn, Even, Load, PhysRAM);
  and and_4 (and_4_out, Even, Store, PhysRAM);
  and and_5 (Ram0_WrEn, and_4_out, Clk);
  assign LO_8 = Rom0_OutEn ? rom_1_data : 8'bz;  // Controlled_Buffer controlled_buffer_1
  and and_6 (Rom1_OutEn, HighByte, Load, PhysROM);
  and and_7 (Ram1_OutEn, HighByte, Load, PhysRAM);
  and and_8 (and_8_out, HighByte, Store, PhysRAM);
  RAM #(.addrWidth(20), .trigger("high")) ram_2 (.addr(PhysAddr[20:1]), .we(Ram1_WrEn), .oe(Ram1_OutEn), .data(HI_8));
  ROM rom_2 (.addr(PhysAddr[8:1]), .data(rom_2_data));
  and and_9 (Ram1_WrEn, and_8_out, Clk);
  and and_10 (and_10_out, Load, Byte, PhysAddr[0]);
  and and_11 (and_11_out, Store, Byte, PhysAddr[0]);
  assign Dout[7:0] = and_10_out ? HI_8 : 8'bz;  // Controlled_Buffer controlled_buffer_2
  assign HI_8 = and_11_out ? Din[7:0] : 8'bz;  // Controlled_Buffer controlled_buffer_3
  assign HI_8 = Rom1_OutEn ? rom_2_data : 8'bz;  // Controlled_Buffer controlled_buffer_4
  transceiver transceiver_1 (
    .Ain(LO_8), .Aout(LO_8), .Bout(Dout[7:0]), .Bin(Din[7:0]), .DirAtoB(Load), .notOE(PhysAddr[0]));
  transceiver transceiver_2 (.Ain(HI_8), .Aout(HI_8), .Bout(Dout[15:8]), .Bin(Din[15:8]), .DirAtoB(Load), .notOE(Byte));
  // Probe on Din

  // Other names for the same wires on the sheet: Odd = PhysAddr[0]; PhysIO = PhysAddr[20]; SignExt = Data

  // Notes on the sheet:
  //   MMIO (RAM / ROM, IO)
  //   Inputs
  //   Logical Wires
  //   Address Range Test
  //   contents of rom_1 (hex, n*v repeats v):
  //   f8 0 66 124*0 f
  //   Chip R/W Select
  //   RAM / ROM
  //   contents of rom_2 (hex, n*v repeats v):
  //   f5 1 77 f0 123*0 e
  //   Needs to be converted
endmodule

module transceiver (
  input  DirAtoB,
  input  notOE,
  input  [7:0] Ain,
  input  [7:0] Bin,
  output [7:0] Bout,
  output [7:0] Aout
);

  wire and_1_out, and_2_out;

  and and_1 (and_1_out, DirAtoB, ~notOE);  // AND_Gate
  assign Bout = and_1_out ? Ain : 8'bz;  // Controlled_Buffer controlled_buffer_1
  assign Aout = and_2_out ? Bin : 8'bz;  // Controlled_Buffer controlled_buffer_2
  and and_2 (and_2_out, ~DirAtoB, ~notOE);  // AND_Gate
endmodule

// MMIO
module mmio (
  input  [15:0] D_IN,
  input  [22:0] PHYS_ADDR,
  input  IO_LOAD,
  input  IO_STORE,
  input  IO_BYTE,
  input  IO_USER,
  input  IO_DATA,
  input  Clk,
  output [15:0] Dout
);

  wire and_1_out, and_2_out, and_3_out, and_5_out, and_6_out, and_7_out, and_8_out, and_9_out, and_10_out,
       and_11_out, and_12_out, and_13_out, and_14_out, and_15_out, and_16_out, and_17_out, and_18_out,
       and_19_out, and_20_out, comparator_2_eq, comparator_2_gt, comparator_2_lt, HIGH_BYTE, IO,
       KERN_CODE_EN, KERN_CODE_LD, KERN_DATA_HI_EN, KERN_DATA_HI_LD, KERN_DATA_LO_EN, KERN_DATA_LO_LD,
       LOW_BYTE, not_1_out, not_2_out, RAM, ROM, USER_CODE_EN, USER_CODE_LD, USER_DATA_HI_EN,
       USER_DATA_HI_LD, USER_DATA_LO_EN, USER_DATA_LO_LD, WORD;
  wire [7:0] HI_8, LO_8;

  or or_1 (HIGH_BYTE, PHYS_ADDR[0], WORD);
  not not_1 (not_1_out, PHYS_ADDR[0]);
  not not_2 (not_2_out, IO_BYTE);
  and and_1 (and_1_out, IO_LOAD, IO_BYTE, PHYS_ADDR[0], IO_DATA);
  and and_2 (and_2_out, IO_STORE, IO_BYTE, PHYS_ADDR[0], IO_DATA);
  not not_3 (WORD, IO_BYTE);
  or or_2 (LOW_BYTE, not_1_out, not_2_out);
  assign Dout[7:0] = and_1_out ? HI_8 : 8'bz;  // Controlled_Buffer controlled_buffer_1
  assign HI_8 = and_2_out ? D_IN[7:0] : 8'bz;  // Controlled_Buffer controlled_buffer_2
  and and_3 (and_3_out, IO_BYTE, PHYS_ADDR[0], IO_DATA);
  transceiver transceiver_1 (
    .Ain(LO_8), .Aout(LO_8), .Bout(Dout[7:0]), .Bin(D_IN[7:0]), .DirAtoB(IO_LOAD), .notOE(and_3_out));
  transceiver transceiver_2 (
    .Ain(HI_8), .Aout(HI_8), .Bout(Dout[15:8]), .Bin(D_IN[15:8]), .DirAtoB(IO_LOAD), .notOE(IO_BYTE));
  // Probe on D_IN
  Comparator #(.width(23)) comparator_1 (.a(PHYS_ADDR), .b(23'h400), .lt(ROM));  // open: gt, eq
  Comparator #(.width(23)) comparator_2 (
    .a(PHYS_ADDR), .b(23'hfc00), .gt(comparator_2_gt), .eq(comparator_2_eq), .lt(comparator_2_lt));
  or or_3 (IO, comparator_2_gt, comparator_2_eq);
  and and_4 (RAM, comparator_2_lt, ~ROM);  // AND_Gate
  and and_5 (and_5_out, RAM, KERN_CODE_LD);
  and and_6 (and_6_out, RAM, KERN_CODE_EN);
  and and_7 (and_7_out, ROM, KERN_CODE_EN);
  ram_64Kx8 ram_64kx8_1 (.A_IN(PHYS_ADDR[15:0]), .D_OUT(LO_8), .WR_EN(and_5_out), .OUT_EN(and_6_out), .CLK(Clk));
  rom_1Kx8 rom_1kx8_1 (.A_IN(PHYS_ADDR[9:0]), .D_OUT(LO_8), .EN(and_7_out));
  ram_2Mx8 ram_2mx8_1 (.A_IN(PHYS_ADDR[20:0]), .D_OUT(LO_8), .WR_EN(USER_CODE_LD), .OUT_EN(USER_CODE_EN), .CLK(Clk));
  Decoder #(.select(2)) decoder_1 (
    .out0(KERN_CODE_EN), .out1(USER_CODE_EN), .out2(KERN_DATA_LO_EN), .out3(USER_DATA_LO_EN),
    .sel({IO_DATA, IO_USER}), .en(and_8_out));
  and and_8 (and_8_out, IO_LOAD, LOW_BYTE);
  Decoder #(.select(2)) decoder_2 (
    .out0(KERN_CODE_LD), .out1(USER_CODE_LD), .out2(KERN_DATA_LO_LD), .out3(USER_DATA_LO_LD),
    .sel({IO_DATA, IO_USER}), .en(and_9_out));
  and and_9 (and_9_out, IO_STORE, LOW_BYTE);
  and and_10 (and_10_out, RAM, KERN_CODE_LD);
  and and_11 (and_11_out, RAM, KERN_CODE_EN);
  and and_12 (and_12_out, ROM, KERN_CODE_EN);
  ram_64Kx8 ram_64kx8_2 (.A_IN(PHYS_ADDR[15:0]), .D_OUT(HI_8), .WR_EN(and_10_out), .OUT_EN(and_11_out), .CLK(Clk));
  rom_1Kx8 rom_1kx8_2 (.A_IN(PHYS_ADDR[9:0]), .D_OUT(HI_8), .EN(and_12_out));
  ram_2Mx8 ram_2mx8_2 (.A_IN(PHYS_ADDR[20:0]), .D_OUT(HI_8), .WR_EN(USER_CODE_LD), .OUT_EN(USER_CODE_EN), .CLK(Clk));
  and and_13 (and_13_out, RAM, KERN_DATA_HI_LD);
  and and_14 (and_14_out, RAM, KERN_DATA_HI_EN);
  and and_15 (and_15_out, ROM, KERN_DATA_LO_EN);
  and and_16 (and_16_out, IO_STORE, HIGH_BYTE);
  ram_32Kx8 ram_32kx8_1 (.A_IN(PHYS_ADDR[15:1]), .D_OUT(LO_8), .WR_EN(and_13_out), .OUT_EN(and_14_out), .CLK(Clk));
  ram_1Mx8 ram_1mx8_1 (
    .A_IN(PHYS_ADDR[20:1]), .WR_EN(USER_DATA_LO_LD), .OUT_EN(USER_DATA_LO_EN), .CLK(Clk), .D_OUT(LO_8));
  rom_512x8 rom_512x8_1 (.A_IN(PHYS_ADDR[9:1]), .D_OUT(LO_8), .EN(and_15_out));
  Decoder #(.select(2)) decoder_3 (
    .out2(KERN_DATA_HI_EN), .out3(USER_DATA_HI_EN), .sel({IO_DATA, IO_USER}), .en(and_17_out));  // open: out0, out1
  and and_17 (and_17_out, IO_LOAD, HIGH_BYTE);
  Decoder #(.select(2)) decoder_4 (
    .out2(KERN_DATA_HI_LD), .out3(USER_DATA_HI_LD), .sel({IO_DATA, IO_USER}), .en(and_16_out));  // open: out0, out1
  and and_18 (and_18_out, RAM, KERN_DATA_HI_LD);
  and and_19 (and_19_out, RAM, KERN_DATA_HI_EN);
  and and_20 (and_20_out, ROM, KERN_DATA_HI_EN);
  ram_32Kx8 ram_32kx8_2 (.A_IN(PHYS_ADDR[15:1]), .D_OUT(HI_8), .WR_EN(and_18_out), .OUT_EN(and_19_out), .CLK(Clk));
  ram_1Mx8 ram_1mx8_2 (
    .A_IN(PHYS_ADDR[20:1]), .WR_EN(USER_DATA_HI_LD), .OUT_EN(USER_DATA_HI_EN), .CLK(Clk), .D_OUT(HI_8));
  rom_512x8 rom_512x8_2 (.A_IN(PHYS_ADDR[9:1]), .D_OUT(HI_8), .EN(and_20_out));

  // Other names for the same wires on the sheet: D_OUT[15:0] = Dout; ODD = PHYS_ADDR[0]

  // Notes on the sheet:
  //   MMIO (RAM, ROM, IO)
  //   Inputs / Outputs
  //   Bus Transceiver (Byte/Word)
  //   Address Range Test (ROM, RAM, or IO?)
  //   Memory (RAM/ROM, Data/Code, User/Kernel)
  //   ...IO devices can fit in here (eg uart, real time clock). IO devices occupy the physical address range 0xfc00 to 0xffff (1 KB).
  //   Load/Store, Hi/Lo, Data/Code, User/Kernel
endmodule

module rom_1Kx8 (
  input  [9:0] A_IN,
  input  EN,
  output [7:0] D_OUT
);

  wire [7:0] rom_1_data;

  ROM #(.addrWidth(10)) rom_1 (.addr(A_IN), .data(rom_1_data));
  assign D_OUT = EN ? rom_1_data : 8'bz;  // Controlled_Buffer controlled_buffer_1
endmodule

module rom_512x8 (
  input  [8:0] A_IN,
  input  EN,
  output [7:0] D_OUT
);

  wire [7:0] rom_1_data;

  ROM #(.addrWidth(9)) rom_1 (.addr(A_IN), .data(rom_1_data));
  assign D_OUT = EN ? rom_1_data : 8'bz;  // Controlled_Buffer controlled_buffer_1
endmodule

module ram_64Kx8 (
  input  [15:0] A_IN,
  input  WR_EN,
  input  OUT_EN,
  input  CLK,
  output [7:0] D_OUT
);

  RAM #(.addrWidth(16)) ram_1 (.addr(A_IN), .we(WR_EN), .oe(OUT_EN), .clk(CLK), .data(D_OUT));
endmodule

module ram_32Kx8 (
  input  [14:0] A_IN,
  input  WR_EN,
  input  OUT_EN,
  input  CLK,
  output [7:0] D_OUT
);

  RAM #(.addrWidth(15)) ram_1 (.addr(A_IN), .we(WR_EN), .oe(OUT_EN), .clk(CLK), .data(D_OUT));
endmodule

module ram_1Mx8 (
  input  [19:0] A_IN,
  input  WR_EN,
  input  OUT_EN,
  input  CLK,
  output [7:0] D_OUT
);

  RAM #(.addrWidth(20)) ram_1 (.addr(A_IN), .we(WR_EN), .oe(OUT_EN), .clk(CLK), .data(D_OUT));
endmodule

module ram_2Mx8 (
  input  [20:0] A_IN,
  input  WR_EN,
  input  OUT_EN,
  input  CLK,
  output [7:0] D_OUT
);

  RAM #(.addrWidth(21)) ram_1 (.addr(A_IN), .we(WR_EN), .oe(OUT_EN), .clk(CLK), .data(D_OUT));
endmodule

module reg_tristate_4bit (
  input  [3:0] Din,
  input  LD,
  input  CLK,
  input  RST,
  input  EN,
  output [3:0] Dout,
  output [3:0] out_7
);

  Register #(.width(4)) register_1 (.D(Din), .en(LD), .clk(CLK), .Q(out_7), .clr(RST));
  assign Dout = EN ? out_7 : 4'bz;  // Controlled_Buffer controlled_buffer_1

  // Notes on the sheet:
  //   Tristate Register (4 bit)
endmodule
