// Logisim project cpu_old.circ as structural Verilog: 13 circuits, main circuit main
module main (
  input  IRQ0,
  input  IRQ1,
  input  IRQ2,
  input  IRQ3
);

  wire ALU_EN_D, ALU_IMM16, BYTE, CARRY, Cin, CLK, CLK_low, clock_1_out, clock_3_out, EN_CAUSE, EN_ERET,
       EN_EXC_ADDR, EN_ISR, EN_STATUS, EN_X, IACK, ILLEGAL_MODE, INC_PC, LD_CAUSE, LD_ERET, LD_EXC_ADDR,
       LD_IMM16, LD_INST, LD_ISR, LD_PTB, LD_STATUS, LD_TIMER, LOAD, LOAD_low, LOGICAL_COND, MMU_DATA,
       MMU_SRC, MMU_ST, MODE, NEG, OVER, REG_X_SRC, RESET, STATUS_SRC, STORE, TIME_OUT, VMEM, ZERO;
  wire [2:0] ALU_SEL, SEL_X;
  wire [3:0] CAUSE_HI_4;
  wire [7:0] CAUSE, CAUSE_out_7, PTB, PTB_out_7;
  wire [15:0] A_BUS, ERET_REG_out_7, EXC_ADDR_out_7, IMM16, IMM16_out_7, INST, INST_out_7, ISR_out_7,
       multiplexer_3_out, PC, reg_unit_1_yout, reg_unit_1_zout, STATUS, STATUS_out_7, TIMER_data, V_ADDR;
  wire [15:8] D_BUS;
  wire [23:0] mmu_1_a_phys;

  // Probe on CAUSE_out_7
  Multiplexer #(.width(16), .enable("false")) multiplexer_1 (.in0(PC), .in1(A_BUS), .out(V_ADDR), .sel(MMU_SRC));
  reg_8bit_tristate u_PTB (
    .in_1(CAUSE), .CLK(LD_PTB), .RST(CLK), .out_7(PTB_out_7), .EN(1'b1), .out_6(PTB));  // open: LD
  // Probe on PTB_out_7
  counter_16_bit TIMER (
    .Din({D_BUS, CAUSE}), .LD_TIMER(MODE), .CLK(LD_TIMER), .RST(CLK), .CARRY(TIME_OUT), .DATA(TIMER_data));  // open: DECR
  // Probe on TIMER_data
  reg_8bit_tristate u_CAUSE (
    .in_1({CAUSE_HI_4, IRQ3, IRQ2, IRQ1, IRQ0}), .LD(LD_CAUSE), .CLK(CLK), .RST(RESET), .out_7(CAUSE_out_7),
    .EN(EN_CAUSE), .out_6(CAUSE));
  mmu mmu_1 (
    .Din({D_BUS, CAUSE}), .Ain(V_ADDR), .PTB(PTB), .MMU_ST(MMU_ST), .VMEM(VMEM), .MMU_DATA(MMU_DATA),
    .A_PHYS(mmu_1_a_phys));
  LED led_1 (.in(clock_1_out));
  Clock clock_1 (.out(clock_1_out));
  Multiplexer #(.width(3), .enable("false")) multiplexer_2 (
    .in0(INST[2:0]), .in1(3'b111), .out(SEL_X), .sel(REG_X_SRC));
  // Probe on mmu_1_a_phys
  reg_tristate EXC_ADDR (
    .Din(V_ADDR), .LD(LD_EXC_ADDR), .CLK(CLK), .RST(RESET), .out_7(EXC_ADDR_out_7), .EN(EN_EXC_ADDR),
    .Dout({D_BUS, CAUSE}));
  // Probe on EXC_ADDR_out_7
  io IO (.Din({D_BUS, CAUSE}), .ADDR(mmu_1_a_phys), .STORE(STORE), .LOAD(LOAD), .CLK(CLK), .Dout({D_BUS, CAUSE}));
  ram_data RAM (
    .Din({D_BUS, CAUSE}), .ADDR(mmu_1_a_phys), .STORE(STORE), .LOAD(LOAD), .BYPASS_RAM(1'b1), .BYTE(BYTE),
    .Dout({D_BUS, CAUSE}));
  // Probe on PC
  reg_tristate ERET_REG (
    .Din(PC), .LD(LD_ERET), .CLK(CLK), .RST(RESET), .out_7(ERET_REG_out_7), .EN(EN_ERET),
    .Dout({D_BUS, CAUSE}));
  // Probe on ERET_REG_out_7
  Clock clock_2 (.out(CLK));
  not not_1 (CLK_low, CLK);
  // Probe on IMM16_out_7
  // Probe on INST_out_7
  reg_tristate ISR (
    .Din({D_BUS, CAUSE}), .LD(LD_ISR), .CLK(CLK), .RST(RESET), .out_7(ISR_out_7), .EN(EN_ISR),
    .Dout({D_BUS, CAUSE}));
  // Probe on ISR_out_7
  reg_tristate u_IMM16 (
    .Din({D_BUS, CAUSE}), .LD(LD_IMM16), .CLK(CLK_low), .RST(RESET), .out_7(IMM16_out_7), .EN(1'b1),
    .Dout(IMM16));
  reg_tristate u_INST (
    .Din({D_BUS, CAUSE}), .LD(LD_INST), .CLK(CLK_low), .RST(RESET), .out_7(INST_out_7), .EN(1'b1),
    .Dout({INST[15:13], BYTE, ALU_SEL, INST[8:0]}));
  // control control_1: pin names not known; wires that end beside it: {D_BUS, CAUSE}, STATUS, CAUSE_HI_4, IRQ0, IRQ1, IRQ2, IRQ3, Cin, ALU_EN_D, LOAD_low, EN_X, REG_X_SRC, INC_PC, ALU_IMM16, STORE, LOAD, MMU_DATA, MMU_ST, MMU_SRC, LD_PTB, LD_IMM16, LD_INST, CLK_low, LD_CAUSE, CLK, EN_CAUSE, STATUS_SRC, EN_STATUS, LD_STATUS, LD_EXC_ADDR, EN_EXC_ADDR, LD_ERET, EN_ERET, IACK, LD_TIMER, LD_ISR, EN_ISR, RESET, LOGICAL_COND, ILLEGAL_MODE, MODE, VMEM
  Clock clock_3 (.out(clock_3_out));
  LED led_2 (.in(clock_3_out));
  // Probe on {D_BUS, CAUSE}
  reg_unit reg_unit_1 (
    .Din({D_BUS, CAUSE}), .LOAD_low(LOAD_low), .CLK_low(CLK_low), .SEL_X(SEL_X), .RST(RESET),
    .SEL_Y(INST[5:3]), .INC_PC(INC_PC), .SEL_Z(INST[8:6]), .EN_X(EN_X), .Xout({D_BUS, CAUSE}),
    .Yout(reg_unit_1_yout), .Zout(reg_unit_1_zout), .PCout(PC));
  Multiplexer #(.width(16), .enable("false")) multiplexer_3 (
    .in0({STATUS[15:4], OVER, CARRY, ZERO, NEG}), .in1({D_BUS, CAUSE}), .out(multiplexer_3_out),
    .sel(STATUS_SRC));
  reg_tristate u_STATUS (
    .Din(multiplexer_3_out), .LD(LD_STATUS), .CLK(CLK), .RST(RESET), .out_7(STATUS_out_7), .EN(1'b1),
    .Dout(STATUS));
  // Probe on STATUS_out_7
  assign {D_BUS, CAUSE} = EN_STATUS ? STATUS : 16'bz;  // Controlled_Buffer controlled_buffer_1
  alu_16_bit alu_16_bit_1 (
    .Y(reg_unit_1_yout), .Z(reg_unit_1_zout), .IMM16(IMM16), .IMM16_2(ALU_IMM16), .Cin(Cin),
    .ALU_SEL(ALU_SEL), .EN_D(ALU_EN_D), .out_8({D_BUS, CAUSE}), .out_9(A_BUS), .ZERO(ZERO), .NEG(NEG),
    .Cout(CARRY), .OVERFLOW(OVER));
  Priority_Encoder #(.select(4)) priority_encoder_1 (
    .in12(TIME_OUT), .in13(ILLEGAL_MODE), .in14(MODE), .in15(LOGICAL_COND), .out(CAUSE_HI_4));  // open: in0, in1, in2, in3, in4, in5, in6, in7, in8, in9, in10, in11, gs, en_out, en_in
  // Probe on CAUSE_HI_4

  // Other names for the same wires on the sheet: IRQ_0 = IRQ0; IRQ_1 = IRQ1; IRQ_2 = IRQ2; IRQ_3 = IRQ3;
  //   D_BUS[7:0] = CAUSE; SEL_Y[2:0] = INST[5:3]; SEL_Z[2:0] = INST[8:6]; INST[12:9] = {BYTE, ALU_SEL}

  // Notes on the sheet:
  //   CPU
endmodule

module \reg  (
  input  [15:0] Din,
  input  EN_X_low,
  input  RST,
  input  EN_Y_low,
  input  EN_Z_low,
  input  LOAD_low,
  input  CLK_low,
  output [15:0] Xout,
  output [15:0] Yout,
  output [15:0] Zout,
  output [15:0] out_11
);

  wire nor_1_out, not_1_out, not_2_out, not_3_out;

  nor nor_1 (nor_1_out, EN_X_low, LOAD_low, CLK_low);
  Register #(.width(16)) register_1 (.D(Din), .en(RST), .clk(nor_1_out), .Q(out_11));  // open: clr
  not not_1 (not_1_out, EN_X_low);
  not not_2 (not_2_out, EN_Y_low);
  not not_3 (not_3_out, EN_Z_low);
  assign Xout = not_1_out ? out_11 : 16'bz;  // Controlled_Buffer controlled_buffer_1
  assign Yout = not_2_out ? out_11 : 16'bz;  // Controlled_Buffer controlled_buffer_2
  assign Zout = not_3_out ? out_11 : 16'bz;  // Controlled_Buffer controlled_buffer_3

  // Notes on the sheet:
  //   Single User Register
endmodule

// REG
module reg_unit (
  input  [15:0] Din,
  input  [2:0] SEL_X,
  input  EN_X,
  input  [2:0] SEL_Y,
  input  LOAD_low,
  input  CLK_low,
  input  RST,
  input  INC_PC,
  input  [2:0] SEL_Z,
  output [15:0] Xout,
  output [15:0] Yout,
  output [15:0] Zout,
  output [15:0] PCout
);

  wire decoder_1_out1, decoder_1_out2, decoder_1_out3, decoder_1_out4, decoder_1_out5, decoder_1_out6,
       decoder_1_out7, decoder_2_out1, decoder_2_out2, decoder_2_out3, decoder_2_out4, decoder_2_out5,
       decoder_2_out6, decoder_2_out7, decoder_3_out1, decoder_3_out2, decoder_3_out3, decoder_3_out4,
       decoder_3_out5, decoder_3_out6, decoder_3_out7, not_1_out, not_2_out, not_3_out, not_4_out, not_5_out,
       not_6_out, not_7_out, not_8_out, not_9_out, not_10_out, not_11_out, not_12_out, not_13_out,
       not_14_out, not_15_out, not_16_out, not_17_out, not_18_out, not_19_out, not_20_out, not_21_out;
  wire [15:0] fp_out_11, pc_out_13, r1_out_11, r2_out_11, r3_out_11, ra_out_11, sp_out_11, Xout_t;

  not not_1 (not_1_out, decoder_1_out1);
  not not_2 (not_2_out, decoder_1_out2);
  not not_3 (not_3_out, decoder_1_out3);
  not not_4 (not_4_out, decoder_1_out4);
  not not_5 (not_5_out, decoder_1_out5);
  not not_6 (not_6_out, decoder_1_out6);
  not not_7 (not_7_out, decoder_1_out7);
  Decoder #(.select(3), .enable("false")) decoder_1 (
    .out1(decoder_1_out1), .out2(decoder_1_out2), .out3(decoder_1_out3), .out4(decoder_1_out4),
    .out5(decoder_1_out5), .out6(decoder_1_out6), .out7(decoder_1_out7), .sel(SEL_Y));  // open: out0
  \reg  r2 (
    .Din(Din), .EN_X_low(not_11_out), .EN_Y_low(not_2_out), .EN_Z_low(not_13_out), .LOAD_low(LOAD_low),
    .CLK_low(CLK_low), .RST(RST), .out_11(r2_out_11), .Xout(Xout_t), .Yout(Yout), .Zout(Zout));
  // Probe on r2_out_11
  \reg  fp (
    .Din(Din), .EN_X_low(not_10_out), .EN_Y_low(not_4_out), .EN_Z_low(not_15_out), .LOAD_low(LOAD_low),
    .CLK_low(CLK_low), .RST(RST), .out_11(fp_out_11), .Xout(Xout_t), .Yout(Yout), .Zout(Zout));
  // Probe on fp_out_11
  \reg  ra (
    .Din(Din), .EN_X_low(not_19_out), .EN_Y_low(not_6_out), .EN_Z_low(not_20_out), .LOAD_low(LOAD_low),
    .CLK_low(CLK_low), .RST(RST), .out_11(ra_out_11), .Xout(Xout_t), .Yout(Yout), .Zout(Zout));
  // Probe on ra_out_11
  Decoder #(.select(3), .enable("false")) decoder_2 (
    .out1(decoder_2_out1), .out2(decoder_2_out2), .out3(decoder_2_out3), .out4(decoder_2_out4),
    .out5(decoder_2_out5), .out6(decoder_2_out6), .out7(decoder_2_out7), .sel(SEL_X));  // open: out0
  not not_8 (not_8_out, decoder_2_out5);
  not not_9 (not_9_out, decoder_2_out3);
  not not_10 (not_10_out, decoder_2_out4);
  not not_11 (not_11_out, decoder_2_out2);
  not not_12 (not_12_out, decoder_2_out1);
  not not_13 (not_13_out, decoder_3_out2);
  not not_14 (not_14_out, decoder_3_out3);
  not not_15 (not_15_out, decoder_3_out4);
  not not_16 (not_16_out, decoder_3_out5);
  not not_17 (not_17_out, decoder_3_out1);
  Decoder #(.select(3), .enable("false")) decoder_3 (
    .out1(decoder_3_out1), .out2(decoder_3_out2), .out3(decoder_3_out3), .out4(decoder_3_out4),
    .out5(decoder_3_out5), .out6(decoder_3_out6), .out7(decoder_3_out7), .sel(SEL_Z));  // open: out0
  not not_18 (not_18_out, decoder_2_out7);
  not not_19 (not_19_out, decoder_2_out6);
  not not_20 (not_20_out, decoder_3_out6);
  not not_21 (not_21_out, decoder_3_out7);
  // Probe on r1_out_11
  // Probe on r3_out_11
  // Probe on sp_out_11
  \reg  r1 (
    .Din(Din), .EN_X_low(not_12_out), .EN_Y_low(not_1_out), .EN_Z_low(not_17_out), .LOAD_low(LOAD_low),
    .CLK_low(CLK_low), .RST(RST), .out_11(r1_out_11), .Xout(Xout_t), .Yout(Yout), .Zout(Zout));
  \reg  r3 (
    .Din(Din), .EN_X_low(not_9_out), .EN_Y_low(not_3_out), .EN_Z_low(not_14_out), .LOAD_low(LOAD_low),
    .CLK_low(CLK_low), .RST(RST), .out_11(r3_out_11), .Xout(Xout_t), .Yout(Yout), .Zout(Zout));
  \reg  sp (
    .Din(Din), .EN_X_low(not_8_out), .EN_Y_low(not_5_out), .EN_Z_low(not_16_out), .LOAD_low(LOAD_low),
    .CLK_low(CLK_low), .RST(RST), .out_11(sp_out_11), .Xout(Xout_t), .Yout(Yout), .Zout(Zout));
  reg_pc pc (
    .RST(RST), .INC_PC(INC_PC), .CLK(CLK_low), .PCin(Din), .EN_X_low(not_18_out), .EN_Y_low(not_7_out),
    .EN_Z_low(not_21_out), .LOAD_low(LOAD_low), .out_13(pc_out_13), .Xout(Xout_t), .Yout(Yout), .Zout(Zout),
    .PCout(PCout));
  // Probe on pc_out_13
  Pull_Resistor pull_resistor_1 (.node(Xout_t));
  assign Xout = EN_X ? Xout_t : 16'bz;  // Controlled_Buffer controlled_buffer_1
  Pull_Resistor pull_resistor_2 (.node(Yout));
  Pull_Resistor pull_resistor_3 (.node(Zout));

  // Notes on the sheet:
  //   Full Register Unit
endmodule

// CONTROL
module control (
  input  [15:0] D_BUS,
  input  [15:0] STATUS,
  input  [3:0] CAUSE_HI_4,
  input  IRQ0,
  input  IRQ1,
  input  IRQ2,
  input  IRQ3,
  input  CLK_x,
  input  CLK,
  output LOGICAL_COND,
  output INVALID_MODE,
  output MODE,
  output VMEM,
  output ALU_Cin,
  output STORE,
  output LD_CAUSE,
  output LD_EXC_ADDR,
  output ALU_EN_D,
  output LOAD,
  output EN_CAUSE,
  output EN_EXC_ADDR,
  output MMU_DATA,
  output LD_ERET,
  output STATUS_SRC,
  output LOAD_low,
  output MMU_ST,
  output EN_ERET,
  output EN_STATUS,
  output EN_X,
  output MMU_SRC,
  output IACK,
  output LD_STATUS,
  output REG_X_SRC,
  output LD_TIMER,
  output LD_PTB,
  output INC_PC,
  output LD_ISR,
  output ALU_IMM16,
  output EN_ISR,
  output LD_IMM16,
  output RESET,
  output LD_INST
);

  wire and_1_out, and_2_out, and_3_out, and_4_out, and_5_out, and_6_out, COND_FALSE, COND_INV,
       decoder_1_out1, decoder_1_out2, decoder_1_out3, decoder_1_out4, decoder_1_out5, decoder_1_out6, IRQ,
       KERN_ONLY, LD_MCA, not_1_out, or_1_out, or_2_out, or_3_out, SET_KERN, SET_USER, TRAP;
  wire [1:0] pull_resistor_1_node;
  wire [2:0] COND;
  wire [6:4] rom_2_data;
  wire [7:0] rom_1_data, rom_1_data_2;
  wire [7:2] register_3_q;
  wire [7:7] register_2_q;
  wire [8:0] bit_extender_1_out, multiplexer_1_out, multiplexer_2_out, NEXT, register_1_q;

  Decoder #(.select(3)) decoder_1 (
    .out1(decoder_1_out1), .out2(decoder_1_out2), .out3(decoder_1_out3), .out4(decoder_1_out4),
    .out5(decoder_1_out5), .out6(decoder_1_out6), .sel(COND));  // open: out0, out7, en
  nor nor_1 (LOGICAL_COND, decoder_1_out5, decoder_1_out6);
  and and_1 (and_1_out, decoder_1_out1, STATUS[0]);
  and and_2 (and_2_out, decoder_1_out2, STATUS[1]);
  and and_3 (and_3_out, decoder_1_out3, STATUS[2]);
  and and_4 (and_4_out, decoder_1_out4, STATUS[3]);
  and and_5 (and_5_out, decoder_1_out5, TRAP);
  and and_6 (and_6_out, decoder_1_out6, IRQ);
  or or_1 (or_1_out, CAUSE_HI_4[0], CAUSE_HI_4[1], CAUSE_HI_4[2], CAUSE_HI_4[3]);
  or or_2 (or_2_out, IRQ0, IRQ1, IRQ2, IRQ3, TRAP);
  LED led_1 (.in(CLK_x));
  Multiplexer #(.width(9), .enable("false")) multiplexer_1 (
    .in0(NEXT), .in1(bit_extender_1_out), .out(multiplexer_1_out), .sel(COND_FALSE));
  assign bit_extender_1_out = {{5{CAUSE_HI_4[3]}}, CAUSE_HI_4};  // Bit_Extender bit_extender_1
  and and_7 (TRAP, or_1_out, MODE, STATUS[5]);
  and and_8 (IRQ, or_2_out, MODE, STATUS[5]);
  Pull_Resistor pull_resistor_1 (.node(pull_resistor_1_node));
  Multiplexer #(.width(9), .enable("false")) multiplexer_2 (
    .in0({pull_resistor_1_node, D_BUS[15:9]}), .in1(multiplexer_1_out), .out(multiplexer_2_out), .sel(LD_MCA));
  or or_3 (or_3_out, and_1_out, and_2_out, and_3_out, and_4_out, and_5_out, and_6_out);
  Register #(.width(9)) register_1 (.D(multiplexer_2_out), .clk(CLK_x), .Q(register_1_q));  // open: en, clr
  xor xor_1 (COND_FALSE, or_3_out, COND_INV);
  ROM #(.addrWidth(9), .dataWidth(32)) rom_1 (
    .addr(register_1_q),
    .data({rom_1_data[3:0], LD_STATUS, EN_STATUS, STATUS_SRC, EN_CAUSE, LD_CAUSE, EN_ISR, LD_ISR, LD_TIMER, IACK, EN_ERET, LD_ERET, EN_EXC_ADDR, LD_EXC_ADDR, rom_1_data_2[1:0], LD_PTB, MMU_SRC, MMU_ST, MMU_DATA, LOAD, STORE, INC_PC, ALU_IMM16, REG_X_SRC, EN_X, LOAD_low, ALU_EN_D, ALU_Cin}));
  ROM #(.addrWidth(9), .dataWidth(16)) rom_2 (
    .addr(register_1_q), .data({NEXT, rom_2_data, KERN_ONLY, rom_1_data[6:4]}));
  Pull_Resistor pull_resistor_2 (.node(rom_1_data[7]));
  Register register_2 (
    .D(rom_1_data), .clk(CLK), .Q({register_2_q[7], SET_USER, SET_KERN, COND, COND_INV, LD_MCA}));  // open: en, clr
  not not_1 (not_1_out, MODE);
  and and_9 (RESET, rom_2_data[4], not_1_out);
  Pull_Resistor pull_resistor_3 (.node(rom_1_data_2[7]));
  Register register_3 (
    .D({{6{rom_1_data_2[7]}}, rom_1_data_2[1:0]}), .clk(CLK), .Q({register_3_q, LD_IMM16, LD_INST}));  // open: en, clr
  S_R_Flip_Flop #(.trigger("high")) s_r_ff_1 (
    .S(SET_KERN), .R(SET_USER), .clk(1'b1), .Q(MODE));  // open: reset, Qn, preset
  and and_10 (INVALID_MODE, KERN_ONLY, MODE);

  assign VMEM = STATUS[4];

  // Other names for the same wires on the sheet: Cin = ALU_Cin; NEG = STATUS[0]; ZERO = STATUS[1]; CARRY = STATUS[2];
  //   OVERFLOW = STATUS[3]; EXC = STATUS[5]

  // Notes on the sheet:
  //   Control Unit
  //   contents of rom_1 (hex, n*v repeats v):
  //   34*0 c0000000 0 0 0 c0000000
  //   External Control Lines
  //   Internal Control Lines
  //   ALU
  //   IO
  //   INST
  //   CAUSE
  //   STATUS
  //   REG_UNIT
  //   EXCEPTIONS
endmodule

module alu_4_bit (
  input  [3:0] Ain,
  input  [3:0] Bin,
  input  INV_B,
  input  Cin,
  input  S1,
  input  S0,
  output [3:0] Dout,
  output Cout
);

  wire [3:0] adder_1_out, and_1_out, bit_extender_1_out, or_1_out, xor_1_out, xor_2_out;

  assign bit_extender_1_out = {{3{INV_B}}, INV_B};  // Bit_Extender bit_extender_1
  assign xor_1_out = Bin ^ bit_extender_1_out;  // XOR_Gate xor_1, 4 bits wide
  Adder #(.width(4)) adder_1 (.a(Ain), .b(xor_1_out), .out(adder_1_out), .cin(Cin), .cout(Cout));
  assign and_1_out = Ain & xor_1_out;  // AND_Gate and_1, 4 bits wide
  assign or_1_out = Ain | xor_1_out;  // OR_Gate or_1, 4 bits wide
  assign xor_2_out = Ain ^ xor_1_out;  // XOR_Gate xor_2, 4 bits wide
  Multiplexer #(.select(2), .width(4), .enable("false")) multiplexer_1 (
    .in0(adder_1_out), .in1(and_1_out), .in2(or_1_out), .in3(xor_2_out), .out(Dout), .sel({S1, S0}));

  // Notes on the sheet:
  //   ALU (4 bit segment)
endmodule

// ALU
module alu_16_bit (
  input  [15:0] Y,
  input  [15:0] Z,
  input  [15:0] IMM16,
  input  IMM16_2,
  input  Cin,
  input  [2:0] ALU_SEL,
  input  EN_D,
  output [15:0] out_8,
  output [15:0] out_9,
  output ZERO,
  output NEG,
  output Cout,
  output OVERFLOW
);

  wire ALU_4_BIT_2_cout, ALU_4_BIT_3_cout, ALU_4_BIT_cout, and_1_out, and_2_out, EN_A, not_2_out, not_3_out,
       not_4_out;
  wire [2:0] ALU_4_BIT_4_dout;
  wire [3:0] ALU_4_BIT_2_dout, ALU_4_BIT_3_dout, ALU_4_BIT_dout;
  wire [15:0] multiplexer_1_out;

  Multiplexer #(.width(16), .enable("false")) multiplexer_1 (
    .in0(Z), .in1(IMM16), .out(multiplexer_1_out), .sel(IMM16_2));
  alu_4_bit ALU_4_BIT (
    .Ain(Y[3:0]), .Bin(multiplexer_1_out[3:0]), .INV_B(ALU_SEL[2]), .Cin(Cin), .S1(ALU_SEL[1]),
    .S0(ALU_SEL[0]), .Dout(ALU_4_BIT_dout), .Cout(ALU_4_BIT_cout));
  alu_4_bit ALU_4_BIT_2 (
    .Ain(Y[7:4]), .Bin(multiplexer_1_out[7:4]), .INV_B(ALU_SEL[2]), .Cin(ALU_4_BIT_cout), .S1(ALU_SEL[1]),
    .S0(ALU_SEL[0]), .Dout(ALU_4_BIT_2_dout), .Cout(ALU_4_BIT_2_cout));
  alu_4_bit ALU_4_BIT_3 (
    .Ain(Y[11:8]), .Bin(multiplexer_1_out[11:8]), .INV_B(ALU_SEL[2]), .Cin(ALU_4_BIT_2_cout),
    .S1(ALU_SEL[1]), .S0(ALU_SEL[0]), .Dout(ALU_4_BIT_3_dout), .Cout(ALU_4_BIT_3_cout));
  alu_4_bit ALU_4_BIT_4 (
    .Ain(Y[15:12]), .Bin(multiplexer_1_out[15:12]), .INV_B(ALU_SEL[2]), .Cin(ALU_4_BIT_3_cout),
    .S1(ALU_SEL[1]), .S0(ALU_SEL[0]), .Dout({NEG, ALU_4_BIT_4_dout}), .Cout(Cout));
  not not_1 (EN_A, EN_D);
  not not_2 (not_2_out, NEG);
  not not_3 (not_3_out, Y[15]);
  not not_4 (not_4_out, multiplexer_1_out[15]);
  assign out_9 = EN_A ? {NEG, ALU_4_BIT_4_dout, ALU_4_BIT_3_dout, ALU_4_BIT_2_dout, ALU_4_BIT_dout} : 16'bz;  // Controlled_Buffer controlled_buffer_1
  nor nor_1 (ZERO, ALU_4_BIT_dout[0], ALU_4_BIT_dout[1], ALU_4_BIT_dout[2], ALU_4_BIT_dout[3], ALU_4_BIT_2_dout[0], ALU_4_BIT_2_dout[1], ALU_4_BIT_2_dout[2], ALU_4_BIT_2_dout[3], ALU_4_BIT_3_dout[1], ALU_4_BIT_3_dout[2], ALU_4_BIT_3_dout[3], ALU_4_BIT_4_dout[0], ALU_4_BIT_4_dout[1], ALU_4_BIT_4_dout[2], NEG, ALU_4_BIT_3_dout[0]);
  and and_1 (and_1_out, not_2_out, Y[15], multiplexer_1_out[15]);
  and and_2 (and_2_out, NEG, not_3_out, not_4_out);
  assign out_8 = EN_D ? {NEG, ALU_4_BIT_4_dout, ALU_4_BIT_3_dout, ALU_4_BIT_2_dout, ALU_4_BIT_dout} : 16'bz;  // Controlled_Buffer controlled_buffer_2
  or or_1 (OVERFLOW, and_1_out, and_2_out);

  // Other names for the same wires on the sheet: IMM16_t = IMM16_2

  // Notes on the sheet:
  //   ALU (Full 16 bit)
endmodule

// MMU
module mmu (
  input  [15:0] Din,
  input  [15:0] Ain,
  input  [7:0] PTB,
  input  MMU_ST,
  input  VMEM,
  input  MMU_DATA,
  output [23:0] A_PHYS
);

  wire and_1_out, and_2_out, nor_1_out, nor_2_out, not_1_out, not_2_out;
  wire [0:0] pull_resistor_3_node;
  wire [15:0] ram_1_data;

  not not_1 (not_1_out, MMU_ST);
  RAM #(.addrWidth(13), .dataWidth(16), .trigger("high")) ram_1 (
    .addr({PTB, Ain[15:11]}), .we(nor_1_out), .oe(nor_2_out), .data(ram_1_data));
  nor nor_1 (nor_1_out, MMU_DATA, not_1_out);
  nor nor_2 (nor_2_out, MMU_DATA, MMU_ST);
  RAM #(.addrWidth(13), .dataWidth(16), .trigger("high")) ram_2 (
    .addr({PTB, Ain[15:11]}), .we(and_1_out), .oe(and_2_out), .data(ram_1_data));
  and and_1 (and_1_out, MMU_DATA, MMU_ST);
  and and_2 (and_2_out, MMU_DATA, not_1_out);
  assign A_PHYS[15:0] = not_2_out ? Ain : 16'bz;  // Controlled_Buffer controlled_buffer_1
  not not_2 (not_2_out, VMEM);
  Pull_Resistor pull_resistor_1 (.node(A_PHYS[22:16]));
  Pull_Resistor pull_resistor_2 (.node(ram_1_data));
  Pull_Resistor pull_resistor_3 (.node(pull_resistor_3_node[0]));
  Multiplexer #(.width(23), .disabled("Z")) multiplexer_1 (
    .in0({ram_1_data[10:0], Ain[10:0], pull_resistor_3_node[0]}), .in1({ram_1_data[11:0], Ain[10:0]}),
    .out(A_PHYS[22:0]), .sel(MMU_DATA), .en(VMEM));

  assign A_PHYS[23] = MMU_DATA;

  // Other names for the same wires on the sheet: DATA = MMU_DATA

  // Notes on the sheet:
  //   Memory Management Unit (MMO)
  //   ~DATA & MMU_ST == ~(DATA | ~MMU_ST)
  //   ~DATA & ~MMU_ST == ~(DATA | MMU_ST)
  //   DATA & MMU_ST
  //   DATA & ~MMU_ST
  //   flags
endmodule

// RAM
module ram_data (
  input  [15:0] Din,
  input  [23:0] ADDR,
  input  BYPASS_RAM,
  input  STORE,
  input  LOAD,
  input  BYTE,
  output [15:0] Dout
);

  wire and_2_out, and_3_out, and_4_out, and_5_out, and_6_out, BYPASS_RAM_t, comparator_1_eq, comparator_2_eq,
       MAP_RAM, not_2_out, not_3_out, not_4_out, or_1_out;
  wire [7:0] rom_1_data, rom_2_data;
  wire [15:0] ram_1_data;

  Comparator #(.width(16)) comparator_1 (.a(ADDR[23:8]), .b(16'h1ff), .eq(comparator_1_eq));  // open: gt, lt
  Comparator #(.width(16)) comparator_2 (.a(ADDR[23:8]), .b({16{1'b0}}), .eq(comparator_2_eq));  // open: gt, lt
  not not_1 (MAP_RAM, comparator_1_eq);
  and and_1 (BYPASS_RAM_t, comparator_2_eq, BYPASS_RAM);
  not not_2 (not_2_out, BYPASS_RAM_t);
  and and_2 (and_2_out, not_2_out, MAP_RAM, STORE);
  and and_3 (and_3_out, not_2_out, MAP_RAM, LOAD);
  RAM #(.addrWidth(23), .trigger("high")) ram_1 (
    .addr(ADDR[23:1]), .we(and_2_out), .oe(and_3_out), .data(ram_1_data[7:0]));
  RAM #(.addrWidth(23), .trigger("high")) ram_2 (
    .addr(ADDR[23:1]), .we(and_2_out), .oe(and_3_out), .data(ram_1_data[15:8]));
  ROM rom_1 (.addr(ADDR[8:1]), .data(rom_1_data));
  ROM rom_2 (.addr(ADDR[8:1]), .data(rom_2_data));
  not not_3 (not_3_out, ADDR[0]);
  not not_4 (not_4_out, BYTE);
  and and_4 (and_4_out, not_3_out, BYTE);
  and and_5 (and_5_out, ADDR[0], BYTE);
  Pull_Resistor pull_resistor_1 (.node(ram_1_data[7:0]));
  Pull_Resistor pull_resistor_2 (.node(ram_1_data[15:8]));
  or or_1 (or_1_out, and_4_out, not_4_out);
  Multiplexer #(.width(8), .disabled("Z"), .enable("false")) multiplexer_1 (
    .in1(rom_1_data), .out(ram_1_data[7:0]), .sel(and_6_out));  // open: in0
  Multiplexer #(.width(8), .disabled("Z"), .enable("false")) multiplexer_2 (
    .in1(rom_2_data), .out(ram_1_data[15:8]), .sel(and_6_out));  // open: in0
  assign Dout[7:0] = or_1_out ? ram_1_data[7:0] : 8'bz;  // Controlled_Buffer controlled_buffer_1
  assign Dout[7:0] = and_5_out ? ram_1_data[15:8] : 8'bz;  // Controlled_Buffer controlled_buffer_2
  assign Dout[15:8] = not_4_out ? ram_1_data[15:8] : 8'bz;  // Controlled_Buffer controlled_buffer_3
  and and_6 (and_6_out, BYPASS_RAM_t, MAP_RAM);
  Multiplexer #(.width(16), .disabled("Z"), .enable("false")) multiplexer_3 (
    .in1(Din), .out(ram_1_data), .sel(and_2_out));  // open: in0

  // Notes on the sheet:
  //   Byte Addressable RAM
  //   contents of rom_1 (hex, n*v repeats v):
  //   255*0 ee
  //   contents of rom_2 (hex, n*v repeats v):
  //   15*0 fe 9*0 fe 5*0 fe 12*0 fe
  //   This RAM unit reads unaligned bytes and aligned 16 bit words.
  //   ~BYTE | (BYTE & ADDR_0)
  //   BYTE & ADDR_0
  //   ~BYTE
  //   these muxes are operating as tristate buffers due to a strange logisim bug
endmodule

module reg_pc (
  input  RST,
  input  INC_PC,
  input  CLK,
  input  [15:0] PCin,
  input  EN_X_low,
  input  EN_Y_low,
  input  EN_Z_low,
  input  LOAD_low,
  output [15:0] Xout,
  output [15:0] Yout,
  output [15:0] Zout,
  output [15:0] PCout,
  output [15:0] out_13
);

  wire counter_1_carry, nor_1_out, not_1_out, not_2_out, not_3_out;
  wire [15:15] counter_1_q, pull_resistor_1_node;

  Pull_Resistor pull_resistor_1 (.node(pull_resistor_1_node[15]));
  nor nor_1 (nor_1_out, LOAD_low, EN_X_low);
  Counter #(.width(16), .max('hffff)) counter_1 (
    .clr(RST), .load(nor_1_out), .up(INC_PC), .count(INC_PC), .clk(CLK),
    .D({pull_resistor_1_node[15], PCin[15:1]}), .carry(counter_1_carry), .Q({counter_1_q[15], out_13[15:1]}));
  Pull_Resistor pull_resistor_2 (.node(out_13[0]));
  assign Xout = not_1_out ? out_13 : 16'bz;  // Controlled_Buffer controlled_buffer_1
  not not_1 (not_1_out, EN_X_low);
  assign Yout = not_2_out ? out_13 : 16'bz;  // Controlled_Buffer controlled_buffer_2
  not not_2 (not_2_out, EN_Y_low);
  assign Zout = not_3_out ? out_13 : 16'bz;  // Controlled_Buffer controlled_buffer_3
  not not_3 (not_3_out, EN_Z_low);

  assign PCout = out_13;

  // Notes on the sheet:
  //   Program Counter (PC)
endmodule

module reg_tristate (
  input  [15:0] Din,
  input  LD,
  input  CLK,
  input  RST,
  input  EN,
  output [15:0] Dout,
  output [15:0] out_7
);

  Register #(.width(16)) register_1 (.D(Din), .en(LD), .clk(CLK), .Q(out_7), .clr(RST));
  assign Dout = EN ? out_7 : 16'bz;  // Controlled_Buffer controlled_buffer_1

  // Notes on the sheet:
  //   Single User Register
endmodule

module reg_8bit_tristate (
  input  [7:0] in_1,
  input  LD,
  input  CLK,
  input  RST,
  input  EN,
  output [7:0] out_6,
  output [7:0] out_7
);

  Register register_1 (.D(in_1), .en(LD), .clk(CLK), .Q(out_7), .clr(RST));
  assign out_6 = EN ? out_7 : 8'bz;  // Controlled_Buffer controlled_buffer_1

  // Notes on the sheet:
  //   Tristate Register (8 bit)
endmodule

module counter_16_bit (
  input  [15:0] Din,
  input  DECR,
  input  LD_TIMER,
  input  CLK,
  input  RST,
  output CARRY,
  output [15:0] DATA
);

  wire and_1_out, not_1_out;

  not not_1 (not_1_out, CARRY);
  and and_1 (and_1_out, not_1_out, DECR);
  Counter #(.width(16), .max('hffff)) counter_1 (
    .clr(RST), .load(LD_TIMER), .up(1'b0), .count(and_1_out), .clk(CLK), .D(Din), .carry(CARRY), .Q(DATA));
endmodule

// IO
module io (
  input  [15:0] Din,
  input  [23:0] ADDR,
  input  STORE,
  input  LOAD,
  input  CLK,
  output [15:0] Dout
);

  wire and_1_out, and_2_out, IO_DEV;

  Comparator #(.width(15)) comparator_1 (.a(ADDR[23:9]), .b(15'h1ff), .eq(IO_DEV));  // open: gt, lt
  and and_1 (and_1_out, STORE, IO_DEV);
  and and_2 (and_2_out, IO_DEV, LOAD);

  // Notes on the sheet:
  //   Data RAM - Byte Addressable
endmodule
