// Logisim project register-unit.circ as structural Verilog: 3 circuits, main circuit main
module main (
  input  in_1,
  input  in_2,
  input  in_3,
  input  in_4
);

  wire not_1_out, pull_resistor_1_node, pull_resistor_2_node, pull_resistor_3_node, pull_resistor_4_node,
       pull_resistor_5_node, pull_resistor_7_node, pull_resistor_8_node, pull_resistor_9_node,
       pull_resistor_10_node, pull_resistor_11_node, pull_resistor_12_node;
  wire [2:0] INST_REG_q, pull_resistor_6_node, pull_resistor_13_node;
  wire [15:0] controlled_buffer_1_out, IMM16_REG_q, ram_1_data, REG_UNIT_a_bus_out, REG_UNIT_pc_out,
       REG_UNIT_x_bus_out;
  wire [15:3] INST_REG_q_2;

  // Probe on REG_UNIT_a_bus_out
  RAM #(.addrWidth(16), .dataWidth(16)) ram_1 (
    .addr(REG_UNIT_a_bus_out), .we(in_1), .oe(in_2), .clk(in_3), .data(ram_1_data));
  Register #(.width(16)) IMM16_REG (
    .D(ram_1_data), .en(pull_resistor_2_node), .clk(pull_resistor_1_node), .Q(IMM16_REG_q));  // open: clr
  Pull_Resistor pull_resistor_1 (.node(pull_resistor_1_node));
  Pull_Resistor pull_resistor_2 (.node(pull_resistor_2_node));
  Register #(.width(16)) INST_REG (
    .D(ram_1_data), .en(pull_resistor_4_node), .clk(pull_resistor_3_node), .Q({INST_REG_q_2, INST_REG_q}));  // open: clr
  Pull_Resistor pull_resistor_3 (.node(pull_resistor_3_node));
  Pull_Resistor pull_resistor_4 (.node(pull_resistor_4_node));
  // Probe on ram_1_data
  assign controlled_buffer_1_out = pull_resistor_5_node ? IMM16_REG_q : 16'bz;  // Controlled_Buffer controlled_buffer_1
  Pull_Resistor pull_resistor_5 (.node(pull_resistor_5_node));
  // Probe on REG_UNIT_x_bus_out
  // Probe on controlled_buffer_1_out
  Pull_Resistor pull_resistor_6 (.node(pull_resistor_6_node));
  Pull_Resistor pull_resistor_7 (.node(pull_resistor_7_node));
  Pull_Resistor pull_resistor_8 (.node(pull_resistor_8_node));
  Pull_Resistor pull_resistor_9 (.node(pull_resistor_9_node));
  Pull_Resistor pull_resistor_10 (.node(pull_resistor_10_node));
  RegisterUnit REG_UNIT (
    .DATA_IN(ram_1_data), .EN_A_BUS(pull_resistor_7_node), .EN_Y_BUS(pull_resistor_10_node),
    .EN_X_BUS(pull_resistor_8_node), .LOAD(pull_resistor_9_node), .SEL_REG_A(INST_REG_q),
    .SEL_REG_Y(INST_REG_q_2[6:4]), .SEL_REG_X(pull_resistor_6_node), .CLK(pull_resistor_11_node),
    .A_BUS_OUT(REG_UNIT_a_bus_out), .Y_BUS_OUT(controlled_buffer_1_out), .X_BUS_OUT(REG_UNIT_x_bus_out),
    .PC_OUT(REG_UNIT_pc_out));
  Pull_Resistor pull_resistor_11 (.node(pull_resistor_11_node));
  ALU ALU (
    .X_IN(REG_UNIT_x_bus_out), .Y_IN(controlled_buffer_1_out), .FUNC(pull_resistor_13_node),
    .EN_ALU(pull_resistor_12_node), .OUT(ram_1_data));
  Pull_Resistor pull_resistor_12 (.node(pull_resistor_12_node));
  Pull_Resistor pull_resistor_13 (.node(pull_resistor_13_node));
  assign REG_UNIT_a_bus_out = not_1_out ? REG_UNIT_pc_out : 16'bz;  // Controlled_Buffer controlled_buffer_2
  not not_1 (not_1_out, in_4);

  // Notes on the sheet:
  //   Opcode
  //   My
  //   Mx
endmodule

module RegisterUnit (
  input  EN_A_BUS,
  input  [2:0] SEL_REG_A,
  input  EN_Y_BUS,
  input  [2:0] SEL_REG_Y,
  input  LOAD,
  input  EN_X_BUS,
  input  [2:0] SEL_REG_X,
  input  CLK,
  input  [15:0] DATA_IN,
  output [15:0] A_BUS_OUT,
  output [15:0] Y_BUS_OUT,
  output [15:0] X_BUS_OUT,
  output [15:0] PC_OUT
);

  wire decoder_1_out0, decoder_1_out1, decoder_1_out2, decoder_1_out3, decoder_1_out4, decoder_1_out5,
       decoder_1_out6, decoder_1_out7, decoder_2_out0, decoder_2_out1, decoder_2_out2, decoder_2_out3,
       decoder_2_out4, decoder_2_out5, decoder_2_out6, decoder_2_out7, decoder_3_out0, decoder_3_out1,
       decoder_3_out2, decoder_3_out3, decoder_3_out4, decoder_3_out5, decoder_3_out6, decoder_3_out7,
       decoder_4_out0, decoder_4_out1, decoder_4_out2, decoder_4_out3, decoder_4_out4, decoder_4_out5,
       decoder_4_out6, decoder_4_out7;
  wire [15:0] register_1_q, register_2_q, register_3_q, register_4_q, register_5_q, register_6_q,
       register_8_q;

  Decoder #(.select(3)) decoder_1 (
    .out0(decoder_1_out0), .out1(decoder_1_out1), .out2(decoder_1_out2), .out3(decoder_1_out3),
    .out4(decoder_1_out4), .out5(decoder_1_out5), .out6(decoder_1_out6), .out7(decoder_1_out7),
    .sel(SEL_REG_X), .en(LOAD));
  Decoder #(.select(3)) decoder_2 (
    .out0(decoder_2_out0), .out1(decoder_2_out1), .out2(decoder_2_out2), .out3(decoder_2_out3),
    .out4(decoder_2_out4), .out5(decoder_2_out5), .out6(decoder_2_out6), .out7(decoder_2_out7),
    .sel(SEL_REG_X), .en(EN_X_BUS));
  Register #(.width(16)) register_1 (.D(DATA_IN), .en(decoder_1_out0), .clk(CLK), .Q(register_1_q));  // open: clr
  Register #(.width(16)) register_2 (.D(DATA_IN), .en(decoder_1_out1), .clk(CLK), .Q(register_2_q));  // open: clr
  Register #(.width(16)) register_3 (.D(DATA_IN), .en(decoder_1_out2), .clk(CLK), .Q(register_3_q));  // open: clr
  Register #(.width(16)) register_4 (.D(DATA_IN), .en(decoder_1_out3), .clk(CLK), .Q(register_4_q));  // open: clr
  Register #(.width(16)) register_5 (.D(DATA_IN), .en(decoder_1_out4), .clk(CLK), .Q(register_5_q));  // open: clr
  Register #(.width(16)) register_6 (.D(DATA_IN), .en(decoder_1_out5), .clk(CLK), .Q(register_6_q));  // open: clr
  Register #(.width(16)) register_7 (.D(DATA_IN), .en(decoder_1_out6), .clk(CLK), .Q(PC_OUT));  // open: clr
  Register #(.width(16)) register_8 (.D(DATA_IN), .en(decoder_1_out7), .clk(CLK), .Q(register_8_q));  // open: clr
  assign X_BUS_OUT = decoder_2_out0 ? register_1_q : 16'bz;  // Controlled_Buffer controlled_buffer_1
  assign X_BUS_OUT = decoder_2_out1 ? register_2_q : 16'bz;  // Controlled_Buffer controlled_buffer_2
  assign X_BUS_OUT = decoder_2_out2 ? register_3_q : 16'bz;  // Controlled_Buffer controlled_buffer_3
  assign X_BUS_OUT = decoder_2_out3 ? register_4_q : 16'bz;  // Controlled_Buffer controlled_buffer_4
  assign X_BUS_OUT = decoder_2_out4 ? register_5_q : 16'bz;  // Controlled_Buffer controlled_buffer_5
  assign X_BUS_OUT = decoder_2_out5 ? register_6_q : 16'bz;  // Controlled_Buffer controlled_buffer_6
  assign X_BUS_OUT = decoder_2_out6 ? PC_OUT : 16'bz;  // Controlled_Buffer controlled_buffer_7
  assign X_BUS_OUT = decoder_2_out7 ? register_8_q : 16'bz;  // Controlled_Buffer controlled_buffer_8
  assign Y_BUS_OUT = decoder_4_out0 ? register_1_q : 16'bz;  // Controlled_Buffer controlled_buffer_9
  assign Y_BUS_OUT = decoder_4_out1 ? register_2_q : 16'bz;  // Controlled_Buffer controlled_buffer_10
  assign Y_BUS_OUT = decoder_4_out2 ? register_3_q : 16'bz;  // Controlled_Buffer controlled_buffer_11
  assign Y_BUS_OUT = decoder_4_out3 ? register_4_q : 16'bz;  // Controlled_Buffer controlled_buffer_12
  assign Y_BUS_OUT = decoder_4_out4 ? register_5_q : 16'bz;  // Controlled_Buffer controlled_buffer_13
  assign Y_BUS_OUT = decoder_4_out5 ? register_6_q : 16'bz;  // Controlled_Buffer controlled_buffer_14
  assign Y_BUS_OUT = decoder_4_out6 ? PC_OUT : 16'bz;  // Controlled_Buffer controlled_buffer_15
  assign Y_BUS_OUT = decoder_4_out7 ? register_8_q : 16'bz;  // Controlled_Buffer controlled_buffer_16
  assign A_BUS_OUT = decoder_3_out0 ? register_1_q : 16'bz;  // Controlled_Buffer controlled_buffer_17
  assign A_BUS_OUT = decoder_3_out1 ? register_2_q : 16'bz;  // Controlled_Buffer controlled_buffer_18
  assign A_BUS_OUT = decoder_3_out2 ? register_3_q : 16'bz;  // Controlled_Buffer controlled_buffer_19
  assign A_BUS_OUT = decoder_3_out3 ? register_4_q : 16'bz;  // Controlled_Buffer controlled_buffer_20
  assign A_BUS_OUT = decoder_3_out4 ? register_5_q : 16'bz;  // Controlled_Buffer controlled_buffer_21
  assign A_BUS_OUT = decoder_3_out5 ? register_6_q : 16'bz;  // Controlled_Buffer controlled_buffer_22
  assign A_BUS_OUT = decoder_3_out6 ? PC_OUT : 16'bz;  // Controlled_Buffer controlled_buffer_23
  assign A_BUS_OUT = decoder_3_out7 ? register_8_q : 16'bz;  // Controlled_Buffer controlled_buffer_24
  Decoder #(.select(3)) decoder_3 (
    .out0(decoder_3_out0), .out1(decoder_3_out1), .out2(decoder_3_out2), .out3(decoder_3_out3),
    .out4(decoder_3_out4), .out5(decoder_3_out5), .out6(decoder_3_out6), .out7(decoder_3_out7),
    .sel(SEL_REG_A), .en(EN_A_BUS));
  Decoder #(.select(3)) decoder_4 (
    .out0(decoder_4_out0), .out1(decoder_4_out1), .out2(decoder_4_out2), .out3(decoder_4_out3),
    .out4(decoder_4_out4), .out5(decoder_4_out5), .out6(decoder_4_out6), .out7(decoder_4_out7),
    .sel(SEL_REG_Y), .en(EN_Y_BUS));

  // Notes on the sheet:
  //   X_BUS
  //   Y_BUS
  //   A_BUS
endmodule

module ALU (
  input  [15:0] X_IN,
  input  [15:0] Y_IN,
  input  [2:0] FUNC,
  input  EN_ALU,
  output [15:0] OUT
);

  wire [15:0] adder_1_out, and_1_out, multiplexer_1_out, or_1_out, subtractor_1_out, subtractor_2_out,
       xor_1_out;

  Subtractor #(.width(16)) subtractor_1 (.a(Y_IN), .b(X_IN), .out(subtractor_1_out));  // open: bin, bout
  Subtractor #(.width(16)) subtractor_2 (.a(X_IN), .b(Y_IN), .out(subtractor_2_out));  // open: bin, bout
  Adder #(.width(16)) adder_1 (.a(X_IN), .b(Y_IN), .out(adder_1_out));  // open: cin, cout
  assign xor_1_out = X_IN ^ Y_IN;  // XOR_Gate xor_1, 16 bits wide
  assign or_1_out = X_IN | Y_IN;  // OR_Gate or_1, 16 bits wide
  assign and_1_out = X_IN & Y_IN;  // AND_Gate and_1, 16 bits wide
  Multiplexer #(.select(3), .width(16), .enable("false")) multiplexer_1 (
    .in1(subtractor_1_out), .in2(subtractor_2_out), .in3(adder_1_out), .in4(xor_1_out), .in5(or_1_out),
    .in6(and_1_out), .in7(Y_IN), .out(multiplexer_1_out), .sel(FUNC));  // open: in0
  assign OUT = EN_ALU ? multiplexer_1_out : 16'bz;  // Controlled_Buffer controlled_buffer_1
endmodule
