// Logisim project simple-datapath-with-control.circ as structural Verilog: 1 circuit, main circuit main
module main (
);

  wire and_1_out, clock_1_out;
  wire [7:0] adder_1_out, counter_1_q, multiplexer_1_out, multiplexer_2_out, negator_1_out, ram_1_data,
       register_1_q, register_2_q, register_3_q;
  wire [11:0] rom_1_data;

  and and_1 (and_1_out, ~rom_1_data[11], clock_1_out);  // AND_Gate
  Clock clock_1 (.out(clock_1_out));
  Counter #(.trigger("falling")) counter_1 (.Q(counter_1_q), .clk(and_1_out));  // open: load, D, count, carry, clr
  RAM ram_1 (
    .addr(register_1_q), .data(ram_1_data), .sel(rom_1_data[10]), .clk(and_1_out), .ld(rom_1_data[9]));  // open: clr
  ROM #(.dataWidth(12)) rom_1 (.addr(counter_1_q), .data(rom_1_data));  // open: sel
  // Probe on ram_1_data
  Register register_1 (.D(ram_1_data), .en(rom_1_data[8]), .Q(register_1_q), .clk(and_1_out));  // open: clr
  Register register_2 (.D(ram_1_data), .en(rom_1_data[7]), .Q(register_2_q), .clk(and_1_out));  // open: clr
  Register register_3 (.D(ram_1_data), .en(rom_1_data[6]), .Q(register_3_q), .clk(and_1_out));  // open: clr
  // Probe on multiplexer_1_out
  Multiplexer #(.select(2), .width(8), .enable("false")) multiplexer_1 (
    .in0(register_1_q), .in1(register_2_q), .in2(register_3_q), .in3({8{1'b0}}), .out(multiplexer_1_out),
    .sel(rom_1_data[5:4]));
  // Probe on multiplexer_2_out
  Multiplexer #(.select(2), .width(8), .enable("false")) multiplexer_2 (
    .in0(register_1_q), .in1(register_2_q), .in2(register_3_q), .in3(8'h1), .out(multiplexer_2_out),
    .sel(rom_1_data[3:2]));
  Negator negator_1 (.in(multiplexer_1_out), .out(negator_1_out));
  Adder adder_1 (.a(multiplexer_1_out), .b(multiplexer_2_out), .out(adder_1_out));  // open: cin, cout
  // Probe on ram_1_data
  Multiplexer #(.width(8)) multiplexer_3 (
    .in0(negator_1_out), .in1(adder_1_out), .out(ram_1_data), .sel(rom_1_data[1]), .en(rom_1_data[0]));

  // Notes on the sheet:
  //   Clock
  //   Disable clock
  //   PC
  //   Enable RAM Unit
  //   RAM
  //   12 Bit "Program" ROM
  //   0: Write, 1: Read
  //   contents of rom_1 (hex, n*v repeats v):
  //   680 10f 640 10f 9b 437 800 233*0 680 10f 640 10f 41b 10f 800
  //   Data bus
  //   Enable Register A
  //   Enable Register B
  //   Enable Mem ADDR Register
  //   Fan-out corresponds to 12-bit word in ROM
  //   Registers
  //   Choose ALU Source A (2 bits) ->
  //   <- Choose ALU Source B (2 bits)
  //   0: NOT, 1: Add
  //   Load ALU to data bus
endmodule
