// Logisim project simple-datapath.circ as structural Verilog: 1 circuit, main circuit main
module main (
  input  in_1,
  input  in_2,
  input  in_3,
  input  in_4,
  input  [1:0] in_5,
  input  in_6,
  input  in_7,
  input  in_8,
  input  [1:0] in_9
);

  wire clock_1_out;
  wire [7:0] adder_1_out, multiplexer_1_out, multiplexer_2_out, not_1_out, ram_1_data, register_1_q,
       register_2_q, register_3_q;

  Clock clock_1 (.out(clock_1_out));
  RAM ram_1 (.addr(register_1_q), .data(ram_1_data), .sel(in_2), .clk(clock_1_out), .ld(in_3));  // open: clr
  // Probe on ram_1_data
  Register register_1 (.D(ram_1_data), .en(in_1), .Q(register_1_q), .clk(clock_1_out));  // open: clr
  Register register_2 (.D(ram_1_data), .en(in_4), .Q(register_2_q), .clk(clock_1_out));  // open: clr
  Register register_3 (.D(ram_1_data), .en(in_8), .Q(register_3_q), .clk(clock_1_out));  // open: clr
  // Probe on multiplexer_1_out
  Multiplexer #(.select(2), .width(8), .enable("false")) multiplexer_1 (
    .in0(register_1_q), .in1(register_2_q), .in2(register_3_q), .in3({8{1'b0}}), .out(multiplexer_1_out),
    .sel(in_5));
  // Probe on multiplexer_2_out
  Multiplexer #(.select(2), .width(8), .enable("false")) multiplexer_2 (
    .in0(register_1_q), .in1(register_2_q), .in2(register_3_q), .in3(8'h1), .out(multiplexer_2_out),
    .sel(in_9));
  assign not_1_out = ~multiplexer_1_out;  // NOT_Gate not_1, 8 bits wide
  Multiplexer #(.width(8)) multiplexer_3 (.in0(not_1_out), .in1(adder_1_out), .out(ram_1_data), .sel(in_6), .en(in_7));
  Adder adder_1 (.a(multiplexer_1_out), .b(multiplexer_2_out), .out(adder_1_out));  // open: cin, cout
  // Probe on ram_1_data
endmodule
