// Logisim project statemachine.circ as structural Verilog: 1 circuit, main circuit main
module main (
  input  [7:0] OPCODE
);

  wire clock_1_out, clock_2_out;
  wire [3:0] register_1_q, rom_1_data, rom_1_data_2;
  wire [7:0] register_2_q;

  Clock clock_1 (.out(clock_1_out));
  Clock clock_2 (.out(clock_2_out));
  Register #(.width(4), .trigger("falling")) register_1 (
    .D(rom_1_data), .clk(clock_1_out), .Q(register_1_q));  // open: en, clr
  Register #(.trigger("falling")) register_2 (
    .D(OPCODE), .en(rom_1_data_2[0]), .clk(clock_2_out), .Q(register_2_q));  // open: clr
  ROM #(.addrWidth(12)) rom_1 (.addr({register_2_q, register_1_q}), .data({rom_1_data, rom_1_data_2}));

  // Notes on the sheet:
  //   Example of State Machine (Basis of control unit)
  //   LOAD_OPCODE
  //   NEXT_INDEX
  //   contents of rom_1 (hex, n*v repeats v):
  //   10 20 30 40 1 11*0 10
  //   <- LOAD_OPCODE
  //   If this is high, load the top 8 bits of ROM address
  //   with the value of OPCODE pins
  //   <- The next lower 4 bits of the ROM address
  //   (transitions to next control state within an instruction)
endmodule
