// Logisim project statemachine_with_condition.circ as structural Verilog: 1 circuit, main circuit main
module main (
  input  ZERO
);

  wire and_1_out, clock_1_out;
  wire [3:0] INDEX_REG_q, multiplexer_1_out;
  wire [7:0] OPCODE_REG_q, rom_1_data, rom_2_data;

  Register #(.width(4), .trigger("falling")) INDEX_REG (
    .D(multiplexer_1_out), .clk(clock_1_out), .Q(INDEX_REG_q));  // open: en, clr
  Clock clock_1 (.out(clock_1_out));
  Register #(.trigger("falling")) OPCODE_REG (.Q(OPCODE_REG_q));  // open: D, en, clk, clr
  ROM #(.addrWidth(12)) rom_1 (.addr({OPCODE_REG_q, INDEX_REG_q}), .data(rom_1_data));
  ROM #(.addrWidth(12)) rom_2 (.addr({OPCODE_REG_q, INDEX_REG_q}), .data(rom_2_data));
  and and_1 (and_1_out, rom_1_data[7], ZERO);
  Multiplexer #(.width(4), .enable("false")) multiplexer_1 (
    .in0(rom_2_data[3:0]), .in1(rom_2_data[7:4]), .out(multiplexer_1_out), .sel(and_1_out));

  // Notes on the sheet:
  //   contents of rom_1 (hex, n*v repeats v):
  //   0 0 0 80 9*0 80
  //   contents of rom_2 (hex, n*v repeats v):
  //   c1 c2 c3 c4 0 0 c0 5*0 6d 60
endmodule
