// Logisim project wb_register_io.circ as structural Verilog: 1 circuit, main circuit main
module main (
  input  in_1,
  input  [2:0] in_2,
  input  [7:0] in_3,
  input  [2:0] in_4,
  output [7:0] out_5
);

  wire clock_1_out, decoder_1_out0, decoder_1_out1, decoder_1_out2, decoder_1_out3, decoder_1_out4,
       decoder_1_out5, decoder_1_out6, decoder_1_out7;
  wire [7:0] register_1_q, register_2_q, register_3_q, register_4_q, register_5_q, register_6_q,
       register_7_q, register_8_q;

  Clock clock_1 (.out(clock_1_out));
  Decoder #(.select(3)) decoder_1 (
    .out0(decoder_1_out0), .out1(decoder_1_out1), .out2(decoder_1_out2), .out3(decoder_1_out3),
    .out4(decoder_1_out4), .out5(decoder_1_out5), .out6(decoder_1_out6), .out7(decoder_1_out7), .sel(in_2),
    .en(in_1));
  Register register_1 (.D(in_3), .en(decoder_1_out0), .clk(clock_1_out), .Q(register_1_q));  // open: clr
  Register register_2 (.D(in_3), .en(decoder_1_out1), .clk(clock_1_out), .Q(register_2_q));  // open: clr
  Register register_3 (.D(in_3), .en(decoder_1_out2), .clk(clock_1_out), .Q(register_3_q));  // open: clr
  Register register_4 (.D(in_3), .en(decoder_1_out3), .clk(clock_1_out), .Q(register_4_q));  // open: clr
  Register register_5 (.D(in_3), .en(decoder_1_out4), .clk(clock_1_out), .Q(register_5_q));  // open: clr
  Register register_6 (.D(in_3), .en(decoder_1_out5), .clk(clock_1_out), .Q(register_6_q));  // open: clr
  Register register_7 (.D(in_3), .en(decoder_1_out6), .clk(clock_1_out), .Q(register_7_q));  // open: clr
  Register register_8 (.D(in_3), .en(decoder_1_out7), .clk(clock_1_out), .Q(register_8_q));  // open: clr
  Multiplexer #(.select(3), .width(8), .enable("false")) multiplexer_1 (
    .in0(register_1_q), .in1(register_2_q), .in2(register_3_q), .in3(register_4_q), .in4(register_5_q),
    .in5(register_6_q), .in6(register_7_q), .in7(register_8_q), .out(out_5), .sel(in_4));
endmodule
